// Logisim project schematic.circ as structural Verilog: 1 circuit, main circuit main
module main (
  input  clk,
  input  [31:0] in1,
  input  load,
  output [31:0] out1
);

  wire [1:0] adder_1_out, multiplexer_1_out, register_1_q;
  wire [31:0] adder_2_out, and_1_out, multiplexer_2_out, R1_q, subtractor_1_out, subtractor_2_out;

  Adder #(.width(2)) adder_1 (.a(register_1_q), .b(2'b01), .out(adder_1_out));  // open: cin, cout
  Multiplexer #(.width(2)) multiplexer_1 (.in0(adder_1_out), .in1(2'b00), .out(multiplexer_1_out), .sel(load));
  Register #(.width(2)) register_1 (.D(multiplexer_1_out), .clk(clk), .Q(register_1_q));  // open: en, clr
  Subtractor #(.width(32)) subtractor_1 (.a({32{1'b0}}), .b(R1_q), .out(subtractor_1_out));  // open: bin, bout
  assign and_1_out = R1_q & out1;  // AND_Gate and_1, 32 bits wide
  Subtractor #(.width(32)) subtractor_2 (.a({32{1'b0}}), .b(out1), .out(subtractor_2_out));  // open: bin, bout
  Adder #(.width(32)) adder_2 (.a(out1), .b(R1_q), .out(adder_2_out));  // open: cin, cout
  Multiplexer #(.select(2), .width(32)) multiplexer_2 (
    .in0(subtractor_1_out), .in1(and_1_out), .in2(subtractor_2_out), .in3(adder_2_out),
    .out(multiplexer_2_out), .sel(register_1_q));
  Register #(.width(32)) R2 (.D(multiplexer_2_out), .en(1'b1), .clk(clk), .Q(out1), .clr(1'b0));
  Register #(.width(32)) R1 (.D(in1), .en(load), .clk(clk), .Q(R1_q), .clr(1'b0));
endmodule
