// Logisim project schematic.circ as structural Verilog: 2 circuits, main circuit main
module main (
  input  [31:0] divisor,
  input  [31:0] dividend,
  input  start,
  input  clk,
  output [31:0] quotient,
  output [31:0] remainder,
  output done
);

  wire comparator_2_gt, not_1_out, not_2_out, or_1_out, or_3_out;
  wire [6:0] counter_1_q, multiplexer_1_out;
  wire [31:0] b_q, D_a, D_q, multiplexer_2_out, multiplexer_5_out, or_2_out, shift_1_new_a, shift_1_new_q,
       subtractor_1_out;

  Multiplexer #(.width(7)) multiplexer_1 (.in0({7{1'b0}}), .in1(7'b0100000), .out(multiplexer_1_out), .sel(start));
  Counter #(.max('h7f), .width(7)) counter_1 (
    .load(or_1_out), .up(1'b0), .clk(clk), .D(multiplexer_1_out), .Q(counter_1_q));  // open: clr, count, carry
  or or_1 (or_1_out, start, done);
  assign or_2_out = shift_1_new_q | 32'h1;  // OR_Gate or_2, 32 bits wide
  Subtractor #(.width(32)) subtractor_1 (.a(shift_1_new_a), .b(b_q), .out(subtractor_1_out));  // open: bin, bout
  Register #(.width(32)) q (.D(multiplexer_2_out), .en(or_3_out), .clk(clk), .Q(quotient));  // open: clr
  Multiplexer #(.width(32)) multiplexer_2 (.in0(D_q), .in1(dividend), .out(multiplexer_2_out), .sel(start));
  Multiplexer #(.width(32)) multiplexer_3 (.in0(shift_1_new_q), .in1(or_2_out), .out(D_q), .sel(not_2_out));
  Multiplexer #(.width(32)) multiplexer_4 (.in0(shift_1_new_a), .in1(subtractor_1_out), .out(D_a), .sel(not_2_out));
  shift shift_1 (.q(quotient), .a(remainder), .new_q(shift_1_new_q), .new_a(shift_1_new_a));
  Register #(.width(32)) a (.D(multiplexer_5_out), .en(or_3_out), .clk(clk), .Q(remainder));  // open: clr
  Multiplexer #(.width(32)) multiplexer_5 (.in0(D_a), .in1({32{1'b0}}), .out(multiplexer_5_out), .sel(start));
  Comparator #(.width(7)) comparator_1 (.a({7{1'b0}}), .b(counter_1_q), .eq(done));  // open: gt, lt
  or or_3 (or_3_out, start, not_1_out);
  not not_1 (not_1_out, done);
  Comparator #(.width(32)) comparator_2 (.a(b_q), .b(shift_1_new_a), .gt(comparator_2_gt));  // open: eq, lt
  Register #(.width(32)) b (.D(divisor), .en(start), .clk(clk), .Q(b_q));  // open: clr
  not not_2 (not_2_out, comparator_2_gt);
endmodule

module shift (
  input  [31:0] q,
  input  [31:0] a,
  output [31:0] new_q,
  output [31:0] new_a
);


  assign new_a = {a[30:0], q[31]};
  assign new_q = {q[30:0], 1'b0};
endmodule
