// Logisim project schematic.circ as structural Verilog: 27 circuits, main circuit main
module shift (
  input  [31:0] q,
  input  [31:0] a,
  output [31:0] new_q,
  output [31:0] new_a
);


  assign new_a = {a[30:0], q[31]};
  assign new_q = {q[30:0], 1'b0};
endmodule

module divison (
  input  [31:0] divisor,
  input  [31:0] dividend,
  input  start,
  input  clk,
  input  rst,
  output [31:0] quotient,
  output [31:0] remainder,
  output done
);

  wire comparator_2_gt, not_1_out, not_2_out, or_1_out, or_3_out;
  wire [6:0] counter_1_q, multiplexer_1_out;
  wire [31:0] b_q, D_a, D_q, multiplexer_2_out, multiplexer_5_out, or_2_out, shift_1_new_a, shift_1_new_q,
       subtractor_1_out;

  Multiplexer #(.width(7)) multiplexer_1 (.in0({7{1'b0}}), .in1(7'b0100000), .out(multiplexer_1_out), .sel(start));
  Counter #(.max('h7f), .width(7)) counter_1 (
    .load(or_1_out), .up(1'b0), .clk(clk), .D(multiplexer_1_out), .Q(counter_1_q));  // open: clr, count, carry
  or or_1 (or_1_out, start, done);
  assign or_2_out = shift_1_new_q | 32'h1;  // OR_Gate or_2, 32 bits wide
  Subtractor #(.width(32)) subtractor_1 (.a(shift_1_new_a), .b(b_q), .out(subtractor_1_out));  // open: bin, bout
  Register #(.width(32)) q (.D(multiplexer_2_out), .en(or_3_out), .clk(clk), .Q(quotient), .clr(rst));
  Multiplexer #(.width(32)) multiplexer_2 (.in0(D_q), .in1(dividend), .out(multiplexer_2_out), .sel(start));
  Multiplexer #(.width(32)) multiplexer_3 (.in0(shift_1_new_q), .in1(or_2_out), .out(D_q), .sel(not_2_out));
  Multiplexer #(.width(32)) multiplexer_4 (.in0(shift_1_new_a), .in1(subtractor_1_out), .out(D_a), .sel(not_2_out));
  shift shift_1 (.q(quotient), .a(remainder), .new_q(shift_1_new_q), .new_a(shift_1_new_a));
  Register #(.width(32)) a (.D(multiplexer_5_out), .en(or_3_out), .clk(clk), .Q(remainder), .clr(rst));
  Multiplexer #(.width(32)) multiplexer_5 (.in0(D_a), .in1({32{1'b0}}), .out(multiplexer_5_out), .sel(start));
  Comparator #(.mode("unsigned"), .width(7)) comparator_1 (.a({7{1'b0}}), .b(counter_1_q), .eq(done));  // open: gt, lt
  or or_3 (or_3_out, start, not_1_out);
  not not_1 (not_1_out, done);
  Comparator #(.mode("unsigned"), .width(32)) comparator_2 (
    .a(b_q), .b(shift_1_new_a), .gt(comparator_2_gt));  // open: eq, lt
  Register #(.width(32)) b (.D(divisor), .en(start), .clk(clk), .Q(b_q), .clr(rst));
  not not_2 (not_2_out, comparator_2_gt);
endmodule

module main (
  input  [31:0] b,
  input  [31:0] a,
  input  [3:0] aluop,
  input  output_inverted,
  input  output_inc,
  input  clk,
  input  rst,
  output [31:0] res_high,
  output done,
  output [31:0] res_low
);

  wire adder_2_cout, and_1_out, and_3_out, comparator_1_eq, comparator_2_eq, done_2, done_3, start,
       Sub_Calculator_carry_out;
  wire [0:0] High_Sum;
  wire [31:0] adder_1_out, adder_2_out, and_2_out, CLO_output, CLZ_output, Div_Calculator_quotient,
       Div_Calculator_remainder, High_shift_left, High_shift_right, High_Sub, left_shift_Calculator_res_low,
       multiplexer_1_out, multiplexer_2_out, multiplexer_3_out, multiplexer_4_out, multiplexer_5_out,
       multiply_calculator_res_low, not_1_out, not_2_out, not_3_out, not_4_out, or_1_out, res_high_t,
       right_shift_Calculator_res_low, rotation_Calculator_res_low, Sub, Sum, xor_1_out;

  Comparator #(.width(4)) comparator_1 (.a(aluop), .b(4'b0011), .eq(comparator_1_eq));  // open: gt, lt
  and and_1 (and_1_out, start, comparator_1_eq);
  handle_start change_a_or_b (.a(a), .b(b), .clk(clk), .rst(rst), .aluop(aluop), .start(start));
  Comparator #(.width(4)) comparator_2 (.a(aluop), .b(4'b0010), .eq(comparator_2_eq));  // open: gt, lt
  divison Div_Calculator (
    .divisor(b), .dividend(a), .start(and_1_out), .clk(clk), .rst(rst), .quotient(Div_Calculator_quotient),
    .remainder(Div_Calculator_remainder), .done(done_3));
  assign and_2_out = a & b;  // AND_Gate and_2, 32 bits wide
  assign or_1_out = a | b;  // OR_Gate or_1, 32 bits wide
  assign xor_1_out = a ^ b;  // XOR_Gate xor_1, 32 bits wide
  Multiplexer #(.select(4), .width(32)) multiplexer_1 (
    .in0({{31{1'b0}}, High_Sum[0]}), .in1(High_Sub), .in2(res_high_t), .in3(Div_Calculator_remainder),
    .in4({32{1'b0}}), .in5({32{1'b0}}), .in6({32{1'b0}}), .in7({32{1'b0}}), .in8({32{1'b0}}),
    .in9(High_shift_left), .in10(High_shift_right), .in11(High_shift_right), .in12({32{1'b0}}),
    .out(multiplexer_1_out), .sel(aluop));  // open: in13, in14, in15
  Multiplexer #(.select(4), .width(32)) multiplexer_2 (
    .in0(Sum), .in1(Sub), .in2(multiply_calculator_res_low), .in3(Div_Calculator_quotient), .in4(and_2_out),
    .in5(or_1_out), .in6(xor_1_out), .in7(CLO_output), .in8(CLZ_output), .in9(left_shift_Calculator_res_low),
    .in10(right_shift_Calculator_res_low), .in11(right_shift_Calculator_res_low),
    .in12(rotation_Calculator_res_low), .out(multiplexer_2_out), .sel(aluop));  // open: in13, in14, in15
  and and_3 (and_3_out, start, comparator_2_eq);
  assign not_1_out = ~b;  // NOT_Gate not_1, 32 bits wide
  assign not_2_out = ~a;  // NOT_Gate not_2, 32 bits wide
  assign not_3_out = ~multiplexer_1_out;  // NOT_Gate not_3, 32 bits wide
  assign not_4_out = ~multiplexer_2_out;  // NOT_Gate not_4, 32 bits wide
  Multiplexer #(.width(32)) multiplexer_3 (
    .in0(multiplexer_1_out), .in1(not_3_out), .out(multiplexer_3_out), .sel(output_inverted));
  Carry_Select_Adder Sum_Calculator (.a(a), .b(b), .Carry_in(1'b0), .Carry_out(High_Sum[0]), .Sum(Sum));
  Carry_Select_Adder Sub_Calculator (
    .a(a), .b(not_1_out), .Carry_in(1'b1), .Carry_out(Sub_Calculator_carry_out), .Sum(Sub));
  CLO_circuit CLO_Calculator (.a(a), .count_CLO(CLO_output));
  CLO_circuit CLZ_Calculator (.a(not_2_out), .count_CLO(CLZ_output));
  left_shift left_shift_Calculator (.a(a), .b(b), .res_low(left_shift_Calculator_res_low), .res_high(High_shift_left));
  right_shift right_shift_Calculator (
    .aluop(aluop), .a(a), .b(b), .res_low(right_shift_Calculator_res_low), .res_high(High_shift_right));
  rotate rotation_Calculator (.a(a), .b(b), .res_low(rotation_Calculator_res_low));
  multiply multiply_calculator (
    .a(a), .b(b), .start(and_3_out), .clk(clk), .rst(rst), .res_high(res_high_t),
    .res_low(multiply_calculator_res_low), .done(done_2));
  Multiplexer #(.width(32)) multiplexer_4 (
    .in0(multiplexer_2_out), .in1(not_4_out), .out(multiplexer_4_out), .sel(output_inverted));
  Multiplexer #(.width(32)) multiplexer_5 (.in0({32{1'b0}}), .in1(32'h1), .out(multiplexer_5_out), .sel(output_inc));
  Adder #(.width(32)) adder_1 (
    .a(multiplexer_3_out), .b({32{1'b0}}), .out(adder_1_out), .cin(adder_2_cout));  // open: cout
  Multiplexer #(.width(32)) multiplexer_6 (
    .in0({32{1'b1}}), .in1({32{1'b0}}), .out(High_Sub), .sel(Sub_Calculator_carry_out));
  Adder #(.width(32)) adder_2 (
    .a(multiplexer_4_out), .b(multiplexer_5_out), .out(adder_2_out), .cout(adder_2_cout));  // open: cin
  Multiplexer #(.width(32)) multiplexer_7 (.in0(adder_1_out), .in1({32{1'b0}}), .out(res_high), .sel(rst));
  Multiplexer #(.width(32)) multiplexer_8 (.in0(adder_2_out), .in1({32{1'b0}}), .out(res_low), .sel(rst));
  Multiplexer #(.select(4)) multiplexer_9 (
    .in0(1'b1), .in1(1'b1), .in2(done_2), .in3(done_3), .in4(1'b1), .in5(1'b1), .in6(1'b1), .in7(1'b1),
    .in8(1'b1), .in9(1'b1), .in10(1'b1), .in11(1'b1), .in12(1'b1), .out(done), .sel(aluop));  // open: in13, in14, in15

  // Other names for the same wires on the sheet: increase = output_inc; invert = output_inverted; reset = rst
endmodule

module sign_extended (
  input  sign,
  input  [31:0] a,
  output [63:0] a_extend
);

  wire [31:0] multiplexer_1_out;

  Multiplexer #(.width(32)) multiplexer_1 (.in0({32{1'b0}}), .in1({32{1'b1}}), .out(multiplexer_1_out), .sel(a[31]));
  Multiplexer #(.width(32)) multiplexer_2 (
    .in0({32{1'b0}}), .in1(multiplexer_1_out), .out(a_extend[63:32]), .sel(sign));

  assign a_extend[31:0] = a;
endmodule

module left_shifter_1 (
  input  [63:0] a,
  output [63:0] a_1_left_shift
);


  assign a_1_left_shift = {a[62:0], 1'b0};
endmodule

module right_shifter_1 (
  input  [63:0] a,
  output [63:0] a_1_right_shift
);


  assign a_1_right_shift = {{2{a[63]}}, a[62:1]};
endmodule

module CLO_circuit (
  input  [31:0] a,
  output [31:0] count_CLO
);

  wire and_1_out, and_2_out, and_3_out, and_4_out, and_5_out, and_6_out, and_7_out, and_8_out, and_9_out,
       and_10_out, and_11_out, and_12_out, and_13_out, and_14_out, and_15_out, and_16_out, and_17_out,
       and_18_out, and_19_out, and_20_out, and_21_out, and_22_out, and_23_out, and_24_out, and_25_out,
       and_26_out, and_27_out, and_28_out, and_29_out, and_30_out, and_31_out, and_32_out;
  wire [5:0] multiplexer_1_out, multiplexer_3_out, multiplexer_4_out, multiplexer_5_out, multiplexer_6_out,
       multiplexer_7_out, multiplexer_8_out, multiplexer_9_out, multiplexer_10_out, multiplexer_11_out,
       multiplexer_12_out, multiplexer_13_out, multiplexer_14_out, multiplexer_15_out, multiplexer_16_out,
       multiplexer_17_out, multiplexer_18_out, multiplexer_19_out, multiplexer_20_out, multiplexer_21_out,
       multiplexer_22_out, multiplexer_23_out, multiplexer_24_out, multiplexer_25_out, multiplexer_26_out,
       multiplexer_27_out, multiplexer_28_out, multiplexer_29_out, multiplexer_30_out, multiplexer_31_out,
       multiplexer_32_out;

  and and_1 (and_1_out, a[31], 1'b1);
  and and_2 (and_2_out, a[30], and_1_out);
  and and_3 (and_3_out, a[29], and_2_out);
  and and_4 (and_4_out, a[28], and_3_out);
  and and_5 (and_5_out, a[27], and_4_out);
  and and_6 (and_6_out, a[26], and_5_out);
  and and_7 (and_7_out, a[25], and_6_out);
  and and_8 (and_8_out, a[24], and_7_out);
  and and_9 (and_9_out, a[23], and_8_out);
  and and_10 (and_10_out, a[22], and_9_out);
  and and_11 (and_11_out, a[21], and_10_out);
  and and_12 (and_12_out, a[20], and_11_out);
  and and_13 (and_13_out, a[19], and_12_out);
  and and_14 (and_14_out, a[18], and_13_out);
  and and_15 (and_15_out, a[17], and_14_out);
  and and_16 (and_16_out, a[16], and_15_out);
  and and_17 (and_17_out, a[15], and_16_out);
  and and_18 (and_18_out, a[14], and_17_out);
  and and_19 (and_19_out, a[13], and_18_out);
  and and_20 (and_20_out, a[12], and_19_out);
  and and_21 (and_21_out, a[11], and_20_out);
  and and_22 (and_22_out, a[10], and_21_out);
  and and_23 (and_23_out, a[9], and_22_out);
  and and_24 (and_24_out, a[8], and_23_out);
  and and_25 (and_25_out, a[7], and_24_out);
  and and_26 (and_26_out, a[6], and_25_out);
  and and_27 (and_27_out, a[5], and_26_out);
  and and_28 (and_28_out, a[4], and_27_out);
  and and_29 (and_29_out, a[3], and_28_out);
  and and_30 (and_30_out, a[2], and_29_out);
  and and_31 (and_31_out, a[1], and_30_out);
  and and_32 (and_32_out, a[0], and_31_out);
  Multiplexer #(.width(6)) multiplexer_1 (.in0({6{1'b0}}), .in1(6'b000001), .out(multiplexer_1_out), .sel(and_1_out));
  Multiplexer #(.width(6)) multiplexer_2 (
    .in0(multiplexer_1_out), .in1(multiplexer_3_out), .out(count_CLO[5:0]), .sel(and_2_out));
  Multiplexer #(.width(6)) multiplexer_3 (
    .in0(6'b000010), .in1(multiplexer_4_out), .out(multiplexer_3_out), .sel(and_3_out));
  Multiplexer #(.width(6)) multiplexer_4 (
    .in0(6'b000011), .in1(multiplexer_5_out), .out(multiplexer_4_out), .sel(and_4_out));
  Multiplexer #(.width(6)) multiplexer_5 (
    .in0(6'b000100), .in1(multiplexer_6_out), .out(multiplexer_5_out), .sel(and_5_out));
  Multiplexer #(.width(6)) multiplexer_6 (
    .in0(6'b000101), .in1(multiplexer_7_out), .out(multiplexer_6_out), .sel(and_6_out));
  Multiplexer #(.width(6)) multiplexer_7 (
    .in0(6'b000110), .in1(multiplexer_8_out), .out(multiplexer_7_out), .sel(and_7_out));
  Multiplexer #(.width(6)) multiplexer_8 (
    .in0(6'b000111), .in1(multiplexer_9_out), .out(multiplexer_8_out), .sel(and_8_out));
  Multiplexer #(.width(6)) multiplexer_9 (
    .in0(6'b001000), .in1(multiplexer_10_out), .out(multiplexer_9_out), .sel(and_9_out));
  Multiplexer #(.width(6)) multiplexer_10 (
    .in0(6'b001001), .in1(multiplexer_11_out), .out(multiplexer_10_out), .sel(and_10_out));
  Multiplexer #(.width(6)) multiplexer_11 (
    .in0(6'b001010), .in1(multiplexer_12_out), .out(multiplexer_11_out), .sel(and_11_out));
  Multiplexer #(.width(6)) multiplexer_12 (
    .in0(6'b001011), .in1(multiplexer_13_out), .out(multiplexer_12_out), .sel(and_12_out));
  Multiplexer #(.width(6)) multiplexer_13 (
    .in0(6'b001100), .in1(multiplexer_14_out), .out(multiplexer_13_out), .sel(and_13_out));
  Multiplexer #(.width(6)) multiplexer_14 (
    .in0(6'b001101), .in1(multiplexer_15_out), .out(multiplexer_14_out), .sel(and_14_out));
  Multiplexer #(.width(6)) multiplexer_15 (
    .in0(6'b001110), .in1(multiplexer_16_out), .out(multiplexer_15_out), .sel(and_15_out));
  Multiplexer #(.width(6)) multiplexer_16 (
    .in0(6'b001111), .in1(multiplexer_17_out), .out(multiplexer_16_out), .sel(and_16_out));
  Multiplexer #(.width(6)) multiplexer_17 (
    .in0(6'b010000), .in1(multiplexer_18_out), .out(multiplexer_17_out), .sel(and_17_out));
  Multiplexer #(.width(6)) multiplexer_18 (
    .in0(6'b010001), .in1(multiplexer_19_out), .out(multiplexer_18_out), .sel(and_18_out));
  Multiplexer #(.width(6)) multiplexer_19 (
    .in0(6'b010010), .in1(multiplexer_20_out), .out(multiplexer_19_out), .sel(and_19_out));
  Multiplexer #(.width(6)) multiplexer_20 (
    .in0(6'b010011), .in1(multiplexer_21_out), .out(multiplexer_20_out), .sel(and_20_out));
  Multiplexer #(.width(6)) multiplexer_21 (
    .in0(6'b010100), .in1(multiplexer_22_out), .out(multiplexer_21_out), .sel(and_21_out));
  Multiplexer #(.width(6)) multiplexer_22 (
    .in0(6'b010101), .in1(multiplexer_23_out), .out(multiplexer_22_out), .sel(and_22_out));
  Multiplexer #(.width(6)) multiplexer_23 (
    .in0(6'b010110), .in1(multiplexer_24_out), .out(multiplexer_23_out), .sel(and_23_out));
  Multiplexer #(.width(6)) multiplexer_24 (
    .in0(6'b010111), .in1(multiplexer_25_out), .out(multiplexer_24_out), .sel(and_24_out));
  Multiplexer #(.width(6)) multiplexer_25 (
    .in0(6'b011000), .in1(multiplexer_26_out), .out(multiplexer_25_out), .sel(and_25_out));
  Multiplexer #(.width(6)) multiplexer_26 (
    .in0(6'b011001), .in1(multiplexer_27_out), .out(multiplexer_26_out), .sel(and_26_out));
  Multiplexer #(.width(6)) multiplexer_27 (
    .in0(6'b011010), .in1(multiplexer_28_out), .out(multiplexer_27_out), .sel(and_27_out));
  Multiplexer #(.width(6)) multiplexer_28 (
    .in0(6'b011011), .in1(multiplexer_29_out), .out(multiplexer_28_out), .sel(and_28_out));
  Multiplexer #(.width(6)) multiplexer_29 (
    .in0(6'b011100), .in1(multiplexer_30_out), .out(multiplexer_29_out), .sel(and_29_out));
  Multiplexer #(.width(6)) multiplexer_30 (
    .in0(6'b011101), .in1(multiplexer_31_out), .out(multiplexer_30_out), .sel(and_30_out));
  Multiplexer #(.width(6)) multiplexer_31 (
    .in0(6'b011110), .in1(multiplexer_32_out), .out(multiplexer_31_out), .sel(and_31_out));
  Multiplexer #(.width(6)) multiplexer_32 (
    .in0(6'b011111), .in1(6'b100000), .out(multiplexer_32_out), .sel(and_32_out));

  assign count_CLO[31:6] = {26{1'b0}};
endmodule

module Carry_Select_Adder (
  input  [31:0] a,
  input  [31:0] b,
  input  Carry_in,
  output Carry_out,
  output [31:0] Sum
);

  wire adder_1_cout, adder_2_cout, adder_3_cout, adder_4_cout, adder_5_cout, adder_6_cout, adder_7_cout,
       multiplexer_5_out, multiplexer_6_out;
  wire [7:0] adder_1_out, adder_2_out, adder_3_out, adder_5_out, adder_6_out, adder_7_out;

  Adder adder_1 (.a(a[31:24]), .b(b[31:24]), .out(adder_1_out), .cin(1'b0), .cout(adder_1_cout));
  Adder adder_2 (.a(a[23:16]), .b(b[23:16]), .out(adder_2_out), .cin(1'b0), .cout(adder_2_cout));
  Adder adder_3 (.a(a[15:8]), .b(b[15:8]), .out(adder_3_out), .cin(1'b0), .cout(adder_3_cout));
  Adder adder_4 (.a(a[7:0]), .b(b[7:0]), .out(Sum[7:0]), .cin(Carry_in), .cout(adder_4_cout));
  Multiplexer #(.width(8)) multiplexer_1 (
    .in0(adder_1_out), .in1(adder_5_out), .out(Sum[31:24]), .sel(multiplexer_5_out));
  Multiplexer #(.width(8)) multiplexer_2 (
    .in0(adder_2_out), .in1(adder_6_out), .out(Sum[23:16]), .sel(multiplexer_6_out));
  Multiplexer #(.width(8)) multiplexer_3 (.in0(adder_3_out), .in1(adder_7_out), .out(Sum[15:8]), .sel(adder_4_cout));
  Adder adder_5 (.a(a[31:24]), .b(b[31:24]), .out(adder_5_out), .cin(1'b1), .cout(adder_5_cout));
  Multiplexer multiplexer_4 (.in0(adder_1_cout), .in1(adder_5_cout), .out(Carry_out), .sel(multiplexer_5_out));
  Adder adder_6 (.a(a[23:16]), .b(b[23:16]), .out(adder_6_out), .cin(1'b1), .cout(adder_6_cout));
  Multiplexer multiplexer_5 (.in0(adder_2_cout), .in1(adder_6_cout), .out(multiplexer_5_out), .sel(multiplexer_6_out));
  Adder adder_7 (.a(a[15:8]), .b(b[15:8]), .out(adder_7_out), .cin(1'b1), .cout(adder_7_cout));
  Multiplexer multiplexer_6 (.in0(adder_3_cout), .in1(adder_7_cout), .out(multiplexer_6_out), .sel(adder_4_cout));
endmodule

module left_shifter_2 (
  input  [63:0] a,
  output [63:0] a_2_left_shift
);


  assign a_2_left_shift = {a[61:0], 2'b00};
endmodule

module left_shifter_4 (
  input  [63:0] a,
  output [63:0] a_4_left_shift
);


  assign a_4_left_shift = {a[59:0], 4'b0000};
endmodule

module left_shifter_8 (
  input  [63:0] a,
  output [63:0] a_8_left_shift
);


  assign a_8_left_shift = {a[55:0], {8{1'b0}}};
endmodule

module left_shifter_16 (
  input  [63:0] a,
  output [63:0] a_16_left_shift
);


  assign a_16_left_shift = {a[47:0], {16{1'b0}}};
endmodule

module right_shifter_2 (
  input  [63:0] a,
  output [63:0] a_2_right_shift
);


  assign a_2_right_shift = {a[63:62], a[63:2]};
endmodule

module right_shifter_4 (
  input  [63:0] a,
  output [63:0] a_4_right_shift
);


  assign a_4_right_shift = {a[63:60], a[63:4]};
endmodule

module right_shifter_8 (
  input  [63:0] a,
  output [63:0] a_8_right_shift
);


  assign a_8_right_shift = {a[63:56], a[63:8]};
endmodule

module right_shifter_16 (
  input  [63:0] a,
  output [63:0] a_16_right_shift
);


  assign a_16_right_shift = {a[63:48], a[63:16]};
endmodule

module left_shift (
  input  [31:0] a,
  input  [31:0] b,
  output [31:0] res_low,
  output [31:0] res_high
);

  wire [63:0] left_shift_2_a_2_left_shift, left_shift_4_a_4_left_shift, left_shift_8_a_8_left_shift,
       left_Shift_16_a_16_left_shift, left_shifte_1_a_1_left_shift, multiplexer_1_out, multiplexer_2_out,
       multiplexer_3_out, multiplexer_4_out, shign_extended_a_extend;

  sign_extended shign_extended (.sign(1'b0), .a(a), .a_extend(shign_extended_a_extend));
  left_shifter_1 left_shifte_1 (.a(shign_extended_a_extend), .a_1_left_shift(left_shifte_1_a_1_left_shift));
  Multiplexer #(.width(64)) multiplexer_1 (
    .in0(shign_extended_a_extend), .in1(left_shifte_1_a_1_left_shift), .out(multiplexer_1_out), .sel(b[0]));
  left_shifter_2 left_shift_2 (.a(multiplexer_1_out), .a_2_left_shift(left_shift_2_a_2_left_shift));
  Multiplexer #(.width(64)) multiplexer_2 (
    .in0(multiplexer_1_out), .in1(left_shift_2_a_2_left_shift), .out(multiplexer_2_out), .sel(b[1]));
  Multiplexer #(.width(64)) multiplexer_3 (
    .in0(multiplexer_2_out), .in1(left_shift_4_a_4_left_shift), .out(multiplexer_3_out), .sel(b[2]));
  left_shifter_4 left_shift_4 (.a(multiplexer_2_out), .a_4_left_shift(left_shift_4_a_4_left_shift));
  Multiplexer #(.width(64)) multiplexer_4 (
    .in0(multiplexer_3_out), .in1(left_shift_8_a_8_left_shift), .out(multiplexer_4_out), .sel(b[3]));
  left_shifter_8 left_shift_8 (.a(multiplexer_3_out), .a_8_left_shift(left_shift_8_a_8_left_shift));
  Multiplexer #(.width(64)) multiplexer_5 (
    .in0(multiplexer_4_out), .in1(left_Shift_16_a_16_left_shift), .out({res_high, res_low}), .sel(b[4]));
  left_shifter_16 left_Shift_16 (.a(multiplexer_4_out), .a_16_left_shift(left_Shift_16_a_16_left_shift));
endmodule

module right_shift (
  input  [3:0] aluop,
  input  [31:0] a,
  input  [31:0] b,
  output [31:0] res_low,
  output [31:0] res_high
);

  wire comparator_1_eq, multiplexer_1_out;
  wire [63:0] multiplexer_2_out, multiplexer_3_out, multiplexer_4_out, multiplexer_5_out,
       right_shift_1_a_1_right_shift, right_shift_2_a_2_right_shift, right_shift_4_a_4_right_shift,
       right_shift_8_a_8_right_shift, right_shift_16_a_16_right_shift, shign_extend_a_extend;

  Comparator #(.width(4)) comparator_1 (.a(aluop), .b(4'b1011), .eq(comparator_1_eq));  // open: gt, lt
  Multiplexer multiplexer_1 (.in0(1'b0), .in1(1'b1), .out(multiplexer_1_out), .sel(comparator_1_eq));
  sign_extended shign_extend (.sign(multiplexer_1_out), .a(a), .a_extend(shign_extend_a_extend));
  right_shifter_1 right_shift_1 (.a(shign_extend_a_extend), .a_1_right_shift(right_shift_1_a_1_right_shift));
  Multiplexer #(.width(64)) multiplexer_2 (
    .in0(shign_extend_a_extend), .in1(right_shift_1_a_1_right_shift), .out(multiplexer_2_out), .sel(b[0]));
  right_shifter_2 right_shift_2 (.a(multiplexer_2_out), .a_2_right_shift(right_shift_2_a_2_right_shift));
  Multiplexer #(.width(64)) multiplexer_3 (
    .in0(multiplexer_2_out), .in1(right_shift_2_a_2_right_shift), .out(multiplexer_3_out), .sel(b[1]));
  right_shifter_4 right_shift_4 (.a(multiplexer_3_out), .a_4_right_shift(right_shift_4_a_4_right_shift));
  Multiplexer #(.width(64)) multiplexer_4 (
    .in0(multiplexer_3_out), .in1(right_shift_4_a_4_right_shift), .out(multiplexer_4_out), .sel(b[2]));
  right_shifter_8 right_shift_8 (.a(multiplexer_4_out), .a_8_right_shift(right_shift_8_a_8_right_shift));
  Multiplexer #(.width(64)) multiplexer_5 (
    .in0(multiplexer_4_out), .in1(right_shift_8_a_8_right_shift), .out(multiplexer_5_out), .sel(b[3]));
  right_shifter_16 right_shift_16 (.a(multiplexer_5_out), .a_16_right_shift(right_shift_16_a_16_right_shift));
  Multiplexer #(.width(64)) multiplexer_6 (
    .in0(multiplexer_5_out), .in1(right_shift_16_a_16_right_shift), .out({res_high, res_low}), .sel(b[4]));
endmodule

module right_rotate_1 (
  input  [31:0] a,
  output [31:0] a_rotate_1
);


  assign a_rotate_1 = {a[0], a[31:1]};
endmodule

module right_rotate_2 (
  input  [31:0] a,
  output [31:0] a_rotate_2
);


  assign a_rotate_2 = {a[1:0], a[31:2]};
endmodule

module right_rotate_4 (
  input  [31:0] a,
  output [31:0] a_rotate_4
);


  assign a_rotate_4 = {a[3:0], a[31:4]};
endmodule

module right_rotate_8 (
  input  [31:0] a,
  output [31:0] a_rotate_8
);


  assign a_rotate_8 = {a[7:0], a[31:8]};
endmodule

module right_rotate_16 (
  input  [31:0] a,
  output [31:0] a_rotate_16
);


  assign a_rotate_16 = {a[15:0], a[31:16]};
endmodule

module rotate (
  input  [31:0] a,
  input  [31:0] b,
  output [31:0] res_low
);

  wire [31:0] multiplexer_1_out, multiplexer_2_out, multiplexer_3_out, multiplexer_4_out,
       rotation_1_a_rotate_1, rotation_2_a_rotate_2, rotation_4_a_rotate_4, rotation_8_a_rotate_8,
       rotation_16_a_rotate_16;

  right_rotate_1 rotation_1 (.a(a), .a_rotate_1(rotation_1_a_rotate_1));
  Multiplexer #(.width(32)) multiplexer_1 (.in0(a), .in1(rotation_1_a_rotate_1), .out(multiplexer_1_out), .sel(b[0]));
  Multiplexer #(.width(32)) multiplexer_2 (
    .in0(multiplexer_1_out), .in1(rotation_2_a_rotate_2), .out(multiplexer_2_out), .sel(b[1]));
  right_rotate_2 rotation_2 (.a(multiplexer_1_out), .a_rotate_2(rotation_2_a_rotate_2));
  Multiplexer #(.width(32)) multiplexer_3 (
    .in0(multiplexer_2_out), .in1(rotation_4_a_rotate_4), .out(multiplexer_3_out), .sel(b[2]));
  right_rotate_4 rotation_4 (.a(multiplexer_2_out), .a_rotate_4(rotation_4_a_rotate_4));
  Multiplexer #(.width(32)) multiplexer_4 (
    .in0(multiplexer_3_out), .in1(rotation_8_a_rotate_8), .out(multiplexer_4_out), .sel(b[3]));
  right_rotate_8 rotation_8 (.a(multiplexer_3_out), .a_rotate_8(rotation_8_a_rotate_8));
  Multiplexer #(.width(32)) multiplexer_5 (
    .in0(multiplexer_4_out), .in1(rotation_16_a_rotate_16), .out(res_low), .sel(b[4]));
  right_rotate_16 rotation_16 (.a(multiplexer_4_out), .a_rotate_16(rotation_16_a_rotate_16));
endmodule

module Carry_Save_Adder (
  input  [31:0] a,
  input  [31:0] b,
  input  [31:0] c,
  output S0,
  output S1,
  output [31:0] new_S
);

  wire adder_33_cout;
  wire [31:0] adder_1_cout, adder_2_out;

  Adder #(.width(1)) adder_1 (.a(a[0]), .b(b[0]), .out(S0), .cin(1'b0), .cout(adder_1_cout[0]));
  Adder #(.width(1)) adder_2 (.a(a[1]), .b(b[1]), .out(adder_2_out[0]), .cin(c[0]), .cout(adder_1_cout[1]));
  Adder #(.width(1)) adder_3 (.a(a[2]), .b(b[2]), .out(adder_2_out[1]), .cin(c[1]), .cout(adder_1_cout[2]));
  Adder #(.width(1)) adder_4 (.a(a[3]), .b(b[3]), .out(adder_2_out[2]), .cin(c[2]), .cout(adder_1_cout[3]));
  Adder #(.width(1)) adder_5 (.a(a[4]), .b(b[4]), .out(adder_2_out[3]), .cin(c[3]), .cout(adder_1_cout[4]));
  Adder #(.width(1)) adder_6 (.a(a[5]), .b(b[5]), .out(adder_2_out[4]), .cin(c[4]), .cout(adder_1_cout[5]));
  Adder #(.width(1)) adder_7 (.a(a[6]), .b(b[6]), .out(adder_2_out[5]), .cin(c[5]), .cout(adder_1_cout[6]));
  Adder #(.width(1)) adder_8 (.a(a[7]), .b(b[7]), .out(adder_2_out[6]), .cin(c[6]), .cout(adder_1_cout[7]));
  Adder #(.width(1)) adder_9 (.a(a[8]), .b(b[8]), .out(adder_2_out[7]), .cin(c[7]), .cout(adder_1_cout[8]));
  Adder #(.width(1)) adder_10 (.a(a[9]), .b(b[9]), .out(adder_2_out[8]), .cin(c[8]), .cout(adder_1_cout[9]));
  Adder #(.width(1)) adder_11 (.a(a[10]), .b(b[10]), .out(adder_2_out[9]), .cin(c[9]), .cout(adder_1_cout[10]));
  Adder #(.width(1)) adder_12 (.a(a[11]), .b(b[11]), .out(adder_2_out[10]), .cin(c[10]), .cout(adder_1_cout[11]));
  Adder #(.width(1)) adder_13 (.a(a[12]), .b(b[12]), .out(adder_2_out[11]), .cin(c[11]), .cout(adder_1_cout[12]));
  Adder #(.width(1)) adder_14 (.a(a[13]), .b(b[13]), .out(adder_2_out[12]), .cin(c[12]), .cout(adder_1_cout[13]));
  Adder #(.width(1)) adder_15 (.a(a[14]), .b(b[14]), .out(adder_2_out[13]), .cin(c[13]), .cout(adder_1_cout[14]));
  Adder #(.width(1)) adder_16 (.a(a[15]), .b(b[15]), .out(adder_2_out[14]), .cin(c[14]), .cout(adder_1_cout[15]));
  Adder #(.width(1)) adder_17 (.a(a[16]), .b(b[16]), .out(adder_2_out[15]), .cin(c[15]), .cout(adder_1_cout[16]));
  Adder #(.width(1)) adder_18 (.a(a[17]), .b(b[17]), .out(adder_2_out[16]), .cin(c[16]), .cout(adder_1_cout[17]));
  Adder #(.width(1)) adder_19 (.a(a[18]), .b(b[18]), .out(adder_2_out[17]), .cin(c[17]), .cout(adder_1_cout[18]));
  Adder #(.width(1)) adder_20 (.a(a[19]), .b(b[19]), .out(adder_2_out[18]), .cin(c[18]), .cout(adder_1_cout[19]));
  Adder #(.width(1)) adder_21 (.a(a[20]), .b(b[20]), .out(adder_2_out[19]), .cin(c[19]), .cout(adder_1_cout[20]));
  Carry_Select_Adder CSA (
    .a(adder_1_cout), .b(adder_2_out), .Carry_in(1'b0), .Carry_out(new_S[31]), .Sum({new_S[30:0], S1}));
  Adder #(.width(1)) adder_22 (.a(a[21]), .b(b[21]), .out(adder_2_out[20]), .cin(c[20]), .cout(adder_1_cout[21]));
  Adder #(.width(1)) adder_23 (.a(a[22]), .b(b[22]), .out(adder_2_out[21]), .cin(c[21]), .cout(adder_1_cout[22]));
  Adder #(.width(1)) adder_24 (.a(a[23]), .b(b[23]), .out(adder_2_out[22]), .cin(c[22]), .cout(adder_1_cout[23]));
  Adder #(.width(1)) adder_25 (.a(a[24]), .b(b[24]), .out(adder_2_out[23]), .cin(c[23]), .cout(adder_1_cout[24]));
  Adder #(.width(1)) adder_26 (.a(a[25]), .b(b[25]), .out(adder_2_out[24]), .cin(c[24]), .cout(adder_1_cout[25]));
  Adder #(.width(1)) adder_27 (.a(a[26]), .b(b[26]), .out(adder_2_out[25]), .cin(c[25]), .cout(adder_1_cout[26]));
  Adder #(.width(1)) adder_28 (.a(a[27]), .b(b[27]), .out(adder_2_out[26]), .cin(c[26]), .cout(adder_1_cout[27]));
  Adder #(.width(1)) adder_29 (.a(a[28]), .b(b[28]), .out(adder_2_out[27]), .cin(c[27]), .cout(adder_1_cout[28]));
  Adder #(.width(1)) adder_30 (.a(a[29]), .b(b[29]), .out(adder_2_out[28]), .cin(c[28]), .cout(adder_1_cout[29]));
  Adder #(.width(1)) adder_31 (.a(a[30]), .b(b[30]), .out(adder_2_out[29]), .cin(c[29]), .cout(adder_1_cout[30]));
  Adder #(.width(1)) adder_32 (.a(a[31]), .b(b[31]), .out(adder_2_out[30]), .cin(c[30]), .cout(adder_1_cout[31]));
  Adder #(.width(1)) adder_33 (.a(1'b0), .b(1'b0), .out(adder_2_out[31]), .cin(c[31]), .cout(adder_33_cout));
endmodule

module multiply (
  input  [31:0] a,
  input  [31:0] b,
  input  start,
  input  clk,
  input  rst,
  output [31:0] res_high,
  output [31:0] res_low,
  output done
);

  wire comparator_1_lt, or_1_out, start_or_done;
  wire [6:0] counter_1_q, multiplexer_1_out;
  wire [31:0] CSA_new_s, multiplexer_2_out, multiplexer_3_out, multiplexer_4_out, multiplexer_5_out,
       multiplexer_6_out, or_3_out, register_1_q;
  wire [31:30] CSA_s0;
  wire [63:0] right_shifter_2_1_a_2_right_shift, right_shifter_2_2_a_2_right_shift;

  Multiplexer #(.width(7)) multiplexer_1 (.in0({7{1'b0}}), .in1(7'b0010000), .out(multiplexer_1_out), .sel(start));
  Counter #(.max('h7f), .width(7)) counter_1 (
    .load(or_1_out), .up(1'b0), .clk(clk), .D(multiplexer_1_out), .Q(counter_1_q));  // open: clr, count, carry
  or or_1 (or_1_out, start, done);
  right_shifter_2 right_shifter_2_1 (
    .a({{32{1'b0}}, register_1_q}), .a_2_right_shift(right_shifter_2_1_a_2_right_shift));
  Multiplexer #(.width(32)) multiplexer_2 (
    .in0(right_shifter_2_1_a_2_right_shift[31:0]), .in1(b), .out(multiplexer_2_out), .sel(start));
  Register #(.width(32)) register_1 (.D(multiplexer_2_out), .en(start_or_done), .clk(clk), .Q(register_1_q), .clr(rst));
  or or_2 (start_or_done, start, comparator_1_lt);
  Comparator #(.mode("unsigned"), .width(7)) comparator_1 (
    .a({7{1'b0}}), .b(counter_1_q), .eq(done), .lt(comparator_1_lt));  // open: gt
  Multiplexer #(.width(32)) multiplexer_3 (.in0({32{1'b0}}), .in1(a), .out(multiplexer_3_out), .sel(register_1_q[0]));
  Multiplexer #(.width(32)) multiplexer_4 (.in0({32{1'b0}}), .in1(a), .out(multiplexer_4_out), .sel(register_1_q[1]));
  right_shifter_2 right_shifter_2_2 (.a({{32{1'b0}}, res_low}), .a_2_right_shift(right_shifter_2_2_a_2_right_shift));
  Carry_Save_Adder CSA (
    .a(res_high), .b(multiplexer_3_out), .c(multiplexer_4_out), .S0(CSA_s0[30]), .S1(CSA_s0[31]),
    .new_S(CSA_new_s));
  assign or_3_out = right_shifter_2_2_a_2_right_shift[31:0] | {CSA_s0, {30{1'b0}}};  // OR_Gate or_3, 32 bits wide
  Multiplexer #(.width(32)) multiplexer_5 (.in0(CSA_new_s), .in1({32{1'b0}}), .out(multiplexer_5_out), .sel(start));
  Multiplexer #(.width(32)) multiplexer_6 (.in0(or_3_out), .in1({32{1'b0}}), .out(multiplexer_6_out), .sel(start));
  Register #(.width(32)) register_2 (.D(multiplexer_5_out), .en(start_or_done), .clk(clk), .Q(res_high), .clr(rst));
  Register #(.width(32)) register_3 (.D(multiplexer_6_out), .en(start_or_done), .clk(clk), .Q(res_low), .clr(rst));
endmodule

module handle_start (
  input  [31:0] a,
  input  [31:0] b,
  input  clk,
  input  rst,
  input  [3:0] aluop,
  output start
);

  wire and_1_out, comparator_1_eq, comparator_2_eq, comparator_3_eq, comparator_4_eq, not_1_out, not_2_out,
       or_1_out, or_2_out;
  wire [31:0] register_1_q, register_2_q;

  Comparator #(.width(4)) comparator_1 (.a(aluop), .b(4'b0010), .eq(comparator_1_eq));  // open: gt, lt
  Comparator #(.width(4)) comparator_2 (.a(aluop), .b(4'b0011), .eq(comparator_2_eq));  // open: gt, lt
  Register #(.width(32)) register_1 (.D(a), .en(1'b1), .clk(clk), .Q(register_1_q), .clr(rst));
  Register #(.width(32)) register_2 (.D(b), .en(1'b1), .clk(clk), .Q(register_2_q), .clr(rst));
  or or_1 (or_1_out, comparator_1_eq, comparator_2_eq);
  Comparator #(.width(32)) comparator_3 (.a(register_1_q), .b(a), .eq(comparator_3_eq));  // open: gt, lt
  Comparator #(.width(32)) comparator_4 (.a(register_2_q), .b(b), .eq(comparator_4_eq));  // open: gt, lt
  not not_1 (not_1_out, comparator_3_eq);
  not not_2 (not_2_out, comparator_4_eq);
  or or_2 (or_2_out, not_1_out, not_2_out);
  and and_1 (and_1_out, or_2_out, or_1_out);
  D_Flip_Flop d_ff_1 (.D(and_1_out), .clk(clk), .Q(start), .reset(rst));  // open: Qn, preset
endmodule
