// Logisim project schematic.circ as structural Verilog: 36 circuits, main circuit main
module main (
  input  Jen,
  input  [31:0] Jin,
  input  rst,
  input  clk,
  output [31:0] R1,
  output [31:0] R2,
  output [31:0] R3,
  output [31:0] R4,
  output [31:0] R5,
  output [31:0] R6,
  output [31:0] R7,
  output [31:0] R8,
  output [31:0] R9,
  output [31:0] R10,
  output [31:0] R11,
  output [31:0] R12,
  output [31:0] R13,
  output [31:0] R14,
  output [31:0] R15,
  output [31:0] R16,
  output [31:0] R17,
  output [31:0] R18,
  output [31:0] R19,
  output [31:0] R20,
  output [31:0] R21,
  output [31:0] R22,
  output [31:0] R23,
  output [31:0] R24,
  output [31:0] R25,
  output [31:0] R26,
  output [31:0] R27,
  output [31:0] R28,
  output [31:0] R29,
  output [31:0] R30,
  output [31:0] R31,
  output [31:0] Jout,
  output InstDone
);

  wire and_1_out, and_2_out, and_7_out, and_8_out, beq, bne, comparator_1_eq, controller_bne,
       controller_jump, controller_mem_write, controller_reg_write, done, Exec, IDecode, IFetch,
       instdone_onehot, is_div, is_jal, is_jr, is_mul, jump, lo_or_hi, Mem, mem_to_reg, mem_write, mf,
       not_1_out, or_1_out, reg_write, regdst, sll_control, slti, source_2, WB;
  wire [3:0] aluop;
  wire [4:0] multiplexer_14_out, multiplexer_15_out, multiplexer_16_out, rs_t, rt;
  wire [5:0] funct, Opcode;
  wire [8:0] adder_1_out, adder_2_out, multiplexer_1_out, multiplexer_3_out, multiplexer_5_out,
       multiplexer_8_out, multiplexer_10_out, multiplexer_12_out, PC, PC_jal;
  wire [15:6] Immediate;
  wire [31:0] a, b, bit_extender_1_out, bit_extender_2_out, bit_extender_4_out, bit_extender_5_out,
       D_MEM_dout, data_read2_q, date_read1, Dwrite, h, hi, I_MEM_dout, jout_t, l, lo, mainALU_res_high,
       mainALU_res_low, multiplexer_2_out, multiplexer_9_out, multiplexer_11_out, multiplexer_13_out,
       multiplexer_17_out, reg_file_dread0, register_2_q, RS;
  wire [63:0] bit_extender_3_out, right_shift_a_2_right_shift;

  or or_1 (or_1_out, Exec, IFetch);
  Register #(.width(9)) register_1 (.D(PC), .en(IDecode), .clk(clk), .Q(PC_jal));  // open: clr
  Register #(.width(9)) PC2 (.D(multiplexer_12_out), .en(or_1_out), .clk(clk), .Q(PC), .clr(rst));
  Adder #(.width(9)) adder_1 (.a(PC), .b(9'h1), .out(adder_1_out));  // open: cin, cout
  handle_inst_done handle_done (
    .done(done), .aluop(aluop), .is_div(is_div), .is_mul(is_mul), .clk(clk), .rst(rst),
    .inst_done(instdone_onehot));
  assign bit_extender_1_out = {{16{Immediate[15]}}, {Immediate, funct}};  // Bit_Extender bit_extender_1
  Adder #(.width(9)) adder_2 (.a(PC), .b({Immediate[8:6], funct}), .out(adder_2_out));  // open: cin, cout
  Comparator #(.mode("unsigned"), .width(32)) comparator_1 (
    .a(l), .b({32{1'b0}}), .eq(comparator_1_eq));  // open: gt, lt
  jtag_ram512 I_MEM (.clk(clk), .Jen(Jen), .Jin(Jin), .Addr(PC), .Jout(jout_t), .Dout(I_MEM_dout));  // open: Din, Wen
  Multiplexer #(.width(9)) multiplexer_1 (.in0(PC), .in1(adder_2_out), .out(multiplexer_1_out), .sel(and_1_out));
  and and_1 (and_1_out, not_1_out, bne);
  not not_1 (not_1_out, comparator_1_eq);
  Control_Unit controller (
    .Opcode(Opcode), .funct(funct), .aluop(aluop), .bne(controller_bne), .source_2(source_2),
    .jump(controller_jump), .regdst(regdst), .mem_to_reg(mem_to_reg), .mf(mf), .lo_or_hi(lo_or_hi),
    .mem_write(controller_mem_write), .reg_write(controller_reg_write), .slti(slti),
    .sll_control(sll_control), .is_div(is_div), .is_jr(is_jr), .is_jal(is_jal), .is_mul(is_mul), .beq(beq));
  Multiplexer #(.width(32)) multiplexer_2 (
    .in0(date_read1), .in1(bit_extender_1_out), .out(multiplexer_2_out), .sel(source_2));
  assign bit_extender_2_out = {{27{Immediate[10]}}, Immediate[10:6]};  // Bit_Extender bit_extender_2
  Multiplexer #(.width(9)) multiplexer_3 (
    .in0(multiplexer_1_out), .in1(adder_2_out), .out(multiplexer_3_out), .sel(and_2_out));
  and and_2 (and_2_out, comparator_1_eq, beq);
  Onehot OneHT (
    .Instdone(instdone_onehot), .rst(rst), .clk(clk), .IFetch(IFetch), .Exec(Exec), .Mem(Mem), .WB(WB),
    .IDecode(IDecode));
  Register #(.width(32)) data_read1 (.D(reg_file_dread0), .en(IDecode), .clk(clk), .Q(RS));  // open: clr
  Multiplexer #(.width(32)) multiplexer_4 (
    .in0(multiplexer_2_out), .in1(bit_extender_2_out), .out(b), .sel(sll_control));
  Register #(.width(32)) IR (
    .D(I_MEM_dout), .en(IFetch), .clk(clk), .Q({Opcode, rs_t, rt, Immediate, funct}), .clr(rst));
  Multiplexer #(.width(9)) multiplexer_5 (
    .in0(multiplexer_3_out), .in1({Immediate[8:6], funct}), .out(multiplexer_5_out), .sel(jump));
  Multiplexer #(.width(32)) multiplexer_6 (
    .in0(multiplexer_9_out), .in1(bit_extender_4_out), .out(Dwrite), .sel(is_jal));
  and and_3 (bne, Exec, controller_bne);
  Register #(.width(32)) data_read2 (.D(date_read1), .en(IDecode), .clk(clk), .Q(data_read2_q));  // open: clr
  Multiplexer #(.width(32)) multiplexer_7 (.in0(RS), .in1(data_read2_q), .out(a), .sel(sll_control));
  Multiplexer #(.width(9)) multiplexer_8 (.in0(PC), .in1(multiplexer_5_out), .out(multiplexer_8_out), .sel(Exec));
  assign bit_extender_3_out = {{32{l[31]}}, l};  // Bit_Extender bit_extender_3
  Multiplexer #(.width(32)) multiplexer_9 (
    .in0(multiplexer_13_out), .in1(multiplexer_11_out), .out(multiplexer_9_out), .sel(mf));
  assign bit_extender_4_out = {{23{1'b0}}, PC_jal};  // Bit_Extender bit_extender_4
  Multiplexer #(.width(9)) multiplexer_10 (
    .in0(multiplexer_8_out), .in1(RS[8:0]), .out(multiplexer_10_out), .sel(is_jr));
  Multiplexer #(.width(32)) multiplexer_11 (.in0(hi), .in1(lo), .out(multiplexer_11_out), .sel(lo_or_hi));
  and and_4 (jump, Exec, controller_jump);
  and and_5 (mem_write, controller_mem_write, Mem);
  and and_6 (reg_write, controller_reg_write, WB);
  Multiplexer #(.width(9)) multiplexer_12 (
    .in0(multiplexer_10_out), .in1(adder_1_out), .out(multiplexer_12_out), .sel(IFetch));
  Multiplexer #(.width(32)) multiplexer_13 (
    .in0(multiplexer_17_out), .in1(bit_extender_5_out), .out(multiplexer_13_out), .sel(slti));
  right_shifter_2 right_shift (.a(bit_extender_3_out), .a_2_right_shift(right_shift_a_2_right_shift));
  Multiplexer #(.width(5)) multiplexer_14 (.in0(Immediate[15:11]), .in1(rt), .out(multiplexer_14_out), .sel(regdst));
  Multiplexer #(.width(5)) multiplexer_15 (
    .in0(multiplexer_14_out), .in1({5{1'b1}}), .out(multiplexer_15_out), .sel(is_jal));
  ALU mainALU (
    .b(b), .a(a), .aluop(aluop), .output_inverted(1'b0), .output_inc(1'b0), .clk(clk), .rst(rst),
    .res_high(mainALU_res_high), .done(done), .res_low(mainALU_res_low));
  assign bit_extender_5_out = {{31{1'b0}}, l[31]};  // Bit_Extender bit_extender_5
  Multiplexer #(.width(5)) multiplexer_16 (
    .in0({5{1'b0}}), .in1(multiplexer_15_out), .out(multiplexer_16_out), .sel(WB));
  Register #(.width(32)) ALU_High (.D(mainALU_res_high), .en(Exec), .clk(clk), .Q(h));  // open: clr
  Register #(.width(32)) ALU_Low (.D(mainALU_res_low), .en(Exec), .clk(clk), .Q(l));  // open: clr
  Multiplexer #(.width(32)) multiplexer_17 (.in0(l), .in1(register_2_q), .out(multiplexer_17_out), .sel(mem_to_reg));
  D_Flip_Flop d_ff_1 (.D(WB), .clk(clk), .Q(InstDone));  // open: Qn, preset, reset
  and and_7 (and_7_out, InstDone, is_div);
  and and_8 (and_8_out, mem_write, done);
  regfile reg_file (
    .clk(clk), .rst(rst), .Dwrite(Dwrite), .Awrite(multiplexer_16_out), .Aread0(rs_t), .Aread1(rt),
    .Dread0(reg_file_dread0), .Dread1(date_read1), .R1(R1), .R2(R2), .R3(R3), .R4(R4), .R5(R5), .R6(R6),
    .R7(R7), .R8(R8), .R9(R9), .R10(R10), .R11(R11), .R12(R12), .R13(R13), .R14(R14), .R15(R15), .R16(R16),
    .R17(R17), .R18(R18), .R19(R19), .R20(R20), .R21(R21), .R22(R22), .R23(R23), .R24(R24), .R25(R25),
    .R26(R26), .R27(R27), .R28(R28), .R29(R29), .R30(R30), .R31(R31));
  Register #(.width(32)) u_lo (.D(l), .en(and_7_out), .clk(clk), .Q(lo), .clr(rst));
  Register #(.width(32)) u_HI (.D(h), .en(and_7_out), .clk(clk), .Q(hi), .clr(rst));
  jtag_ram512 D_MEM (
    .clk(clk), .Jen(Jen), .Din(date_read1), .Jin(jout_t), .Wen(and_8_out),
    .Addr(right_shift_a_2_right_shift[8:0]), .Jout(Jout), .Dout(D_MEM_dout));
  Register #(.width(32)) register_2 (.D(D_MEM_dout), .en(Mem), .clk(clk), .Q(register_2_q));  // open: clr

  // Other names for the same wires on the sheet: Immediate[5:0] = funct; shamt[4:0] = Immediate[10:6];
  //   rd[4:0] = Immediate[15:11]

  // Notes on the sheet:
  //   Jin: initial=0x8fbf0000
endmodule

module jtag_ram8 (
  input  clk,
  input  Jen,
  input  [31:0] Din,
  input  [31:0] Jin,
  input  Wen,
  input  [2:0] Addr,
  output [31:0] Dout,
  output [31:0] Jout
);

  wire decoder_1_out0, decoder_1_out1, decoder_1_out2, decoder_1_out3, decoder_1_out4, decoder_1_out5,
       decoder_1_out6, decoder_1_out7, or_1_out, or_2_out, or_3_out, or_4_out, or_5_out, or_6_out, or_7_out,
       or_8_out;
  wire [31:0] M0, M1, M2, M3, M4, M5, M6, multiplexer_1_out, multiplexer_2_out, multiplexer_3_out,
       multiplexer_4_out, multiplexer_5_out, multiplexer_6_out, multiplexer_7_out, multiplexer_8_out;

  Decoder #(.select(3)) decoder_1 (
    .out0(decoder_1_out0), .out1(decoder_1_out1), .out2(decoder_1_out2), .out3(decoder_1_out3),
    .out4(decoder_1_out4), .out5(decoder_1_out5), .out6(decoder_1_out6), .out7(decoder_1_out7), .sel(Addr),
    .en(Wen));
  Multiplexer #(.width(32)) multiplexer_1 (.in0(Din), .in1(Jin), .out(multiplexer_1_out), .sel(Jen));
  Multiplexer #(.width(32)) multiplexer_2 (.in0(Din), .in1(M0), .out(multiplexer_2_out), .sel(Jen));
  Multiplexer #(.width(32)) multiplexer_3 (.in0(Din), .in1(M1), .out(multiplexer_3_out), .sel(Jen));
  Multiplexer #(.width(32)) multiplexer_4 (.in0(Din), .in1(M2), .out(multiplexer_4_out), .sel(Jen));
  Multiplexer #(.width(32)) multiplexer_5 (.in0(Din), .in1(M3), .out(multiplexer_5_out), .sel(Jen));
  Multiplexer #(.width(32)) multiplexer_6 (.in0(Din), .in1(M4), .out(multiplexer_6_out), .sel(Jen));
  Multiplexer #(.width(32)) multiplexer_7 (.in0(Din), .in1(M5), .out(multiplexer_7_out), .sel(Jen));
  Multiplexer #(.width(32)) multiplexer_8 (.in0(Din), .in1(M6), .out(multiplexer_8_out), .sel(Jen));
  Register #(.width(32)) register_1 (.D(multiplexer_1_out), .en(or_1_out), .clk(clk), .Q(M0));  // open: clr
  or or_1 (or_1_out, Jen, decoder_1_out0);
  Register #(.width(32)) register_2 (.D(multiplexer_2_out), .en(or_2_out), .clk(clk), .Q(M1));  // open: clr
  or or_2 (or_2_out, Jen, decoder_1_out1);
  Register #(.width(32)) register_3 (.D(multiplexer_3_out), .en(or_3_out), .clk(clk), .Q(M2));  // open: clr
  or or_3 (or_3_out, Jen, decoder_1_out2);
  Register #(.width(32)) register_4 (.D(multiplexer_4_out), .en(or_4_out), .clk(clk), .Q(M3));  // open: clr
  or or_4 (or_4_out, Jen, decoder_1_out3);
  Register #(.width(32)) register_5 (.D(multiplexer_5_out), .en(or_5_out), .clk(clk), .Q(M4));  // open: clr
  or or_5 (or_5_out, Jen, decoder_1_out4);
  Register #(.width(32)) register_6 (.D(multiplexer_6_out), .en(or_6_out), .clk(clk), .Q(M5));  // open: clr
  or or_6 (or_6_out, Jen, decoder_1_out5);
  Register #(.width(32)) register_7 (.D(multiplexer_7_out), .en(or_7_out), .clk(clk), .Q(M6));  // open: clr
  or or_7 (or_7_out, Jen, decoder_1_out6);
  Register #(.width(32)) register_8 (.D(multiplexer_8_out), .en(or_8_out), .clk(clk), .Q(Jout));  // open: clr
  or or_8 (or_8_out, Jen, decoder_1_out7);
  Multiplexer #(.select(3), .width(32)) multiplexer_9 (
    .in0(M0), .in1(M1), .in2(M2), .in3(M3), .in4(M4), .in5(M5), .in6(M6), .in7(Jout), .out(Dout), .sel(Addr));

  // Other names for the same wires on the sheet: M7[31:0] = Jout
endmodule

module jtag_ram64 (
  input  clk,
  input  Jen,
  input  [31:0] Din,
  input  [31:0] Jin,
  input  Wen,
  input  [5:0] Addr,
  output [31:0] Dout,
  output [31:0] Jout
);

  wire decoder_1_out0, decoder_1_out1, decoder_1_out2, decoder_1_out3, decoder_1_out4, decoder_1_out5,
       decoder_1_out6, decoder_1_out7;
  wire [31:0] b0_dout, b0_jout, b1_dout, b1_jout, b2_dout, b2_jout, b3_dout, b3_jout, b4_dout, b4_jout,
       b5_dout, b5_jout, b6_dout, b6_jout, b7_dout;

  Decoder #(.select(3)) decoder_1 (
    .out0(decoder_1_out0), .out1(decoder_1_out1), .out2(decoder_1_out2), .out3(decoder_1_out3),
    .out4(decoder_1_out4), .out5(decoder_1_out5), .out6(decoder_1_out6), .out7(decoder_1_out7),
    .sel(Addr[5:3]), .en(Wen));
  jtag_ram8 b0 (
    .clk(clk), .Jen(Jen), .Din(Din), .Jin(Jin), .Wen(decoder_1_out0), .Addr(Addr[2:0]), .Dout(b0_dout),
    .Jout(b0_jout));
  jtag_ram8 b1 (
    .clk(clk), .Jen(Jen), .Din(Din), .Jin(b0_jout), .Wen(decoder_1_out1), .Addr(Addr[2:0]), .Dout(b1_dout),
    .Jout(b1_jout));
  jtag_ram8 b2 (
    .clk(clk), .Jen(Jen), .Din(Din), .Jin(b1_jout), .Wen(decoder_1_out2), .Addr(Addr[2:0]), .Dout(b2_dout),
    .Jout(b2_jout));
  jtag_ram8 b3 (
    .clk(clk), .Jen(Jen), .Din(Din), .Jin(b2_jout), .Wen(decoder_1_out3), .Addr(Addr[2:0]), .Dout(b3_dout),
    .Jout(b3_jout));
  jtag_ram8 b4 (
    .clk(clk), .Jen(Jen), .Din(Din), .Jin(b3_jout), .Wen(decoder_1_out4), .Addr(Addr[2:0]), .Dout(b4_dout),
    .Jout(b4_jout));
  jtag_ram8 b5 (
    .clk(clk), .Jen(Jen), .Din(Din), .Jin(b4_jout), .Wen(decoder_1_out5), .Addr(Addr[2:0]), .Dout(b5_dout),
    .Jout(b5_jout));
  jtag_ram8 b6 (
    .clk(clk), .Jen(Jen), .Din(Din), .Jin(b5_jout), .Wen(decoder_1_out6), .Addr(Addr[2:0]), .Dout(b6_dout),
    .Jout(b6_jout));
  jtag_ram8 b7 (
    .clk(clk), .Jen(Jen), .Din(Din), .Jin(b6_jout), .Wen(decoder_1_out7), .Addr(Addr[2:0]), .Dout(b7_dout),
    .Jout(Jout));
  Multiplexer #(.select(3), .width(32)) multiplexer_1 (
    .in0(b0_dout), .in1(b1_dout), .in2(b2_dout), .in3(b3_dout), .in4(b4_dout), .in5(b5_dout), .in6(b6_dout),
    .in7(b7_dout), .out(Dout), .sel(Addr[5:3]));
endmodule

module jtag_ram512 (
  input  clk,
  input  Jen,
  input  [31:0] Din,
  input  [31:0] Jin,
  input  Wen,
  input  [8:0] Addr,
  output [31:0] Jout,
  output [31:0] Dout
);

  wire decoder_1_out0, decoder_1_out1, decoder_1_out2, decoder_1_out3, decoder_1_out4, decoder_1_out5,
       decoder_1_out6, decoder_1_out7;
  wire [31:0] b0_dout, b0_jout, b1_dout, b1_jout, b2_dout, b2_jout, b3_dout, b3_jout, b4_dout, b4_jout,
       b5_dout, b5_jout, b6_dout, b6_jout, b7_dout;

  Decoder #(.select(3)) decoder_1 (
    .out0(decoder_1_out0), .out1(decoder_1_out1), .out2(decoder_1_out2), .out3(decoder_1_out3),
    .out4(decoder_1_out4), .out5(decoder_1_out5), .out6(decoder_1_out6), .out7(decoder_1_out7),
    .sel(Addr[8:6]), .en(Wen));
  jtag_ram64 b0 (
    .clk(clk), .Jen(Jen), .Din(Din), .Jin(Jin), .Wen(decoder_1_out0), .Addr(Addr[5:0]), .Dout(b0_dout),
    .Jout(b0_jout));
  jtag_ram64 b1 (
    .clk(clk), .Jen(Jen), .Din(Din), .Jin(b0_jout), .Wen(decoder_1_out1), .Addr(Addr[5:0]), .Dout(b1_dout),
    .Jout(b1_jout));
  jtag_ram64 b2 (
    .clk(clk), .Jen(Jen), .Din(Din), .Jin(b1_jout), .Wen(decoder_1_out2), .Addr(Addr[5:0]), .Dout(b2_dout),
    .Jout(b2_jout));
  jtag_ram64 b3 (
    .clk(clk), .Jen(Jen), .Din(Din), .Jin(b2_jout), .Wen(decoder_1_out3), .Addr(Addr[5:0]), .Dout(b3_dout),
    .Jout(b3_jout));
  jtag_ram64 b4 (
    .clk(clk), .Jen(Jen), .Din(Din), .Jin(b3_jout), .Wen(decoder_1_out4), .Addr(Addr[5:0]), .Dout(b4_dout),
    .Jout(b4_jout));
  jtag_ram64 b5 (
    .clk(clk), .Jen(Jen), .Din(Din), .Jin(b4_jout), .Wen(decoder_1_out5), .Addr(Addr[5:0]), .Dout(b5_dout),
    .Jout(b5_jout));
  jtag_ram64 b6 (
    .clk(clk), .Jen(Jen), .Din(Din), .Jin(b5_jout), .Wen(decoder_1_out6), .Addr(Addr[5:0]), .Dout(b6_dout),
    .Jout(b6_jout));
  jtag_ram64 b7 (
    .clk(clk), .Jen(Jen), .Din(Din), .Jin(b6_jout), .Wen(decoder_1_out7), .Addr(Addr[5:0]), .Dout(b7_dout),
    .Jout(Jout));
  Multiplexer #(.select(3), .width(32)) multiplexer_1 (
    .in0(b0_dout), .in1(b1_dout), .in2(b2_dout), .in3(b3_dout), .in4(b4_dout), .in5(b5_dout), .in6(b6_dout),
    .in7(b7_dout), .out(Dout), .sel(Addr[8:6]));
endmodule

module regfile (
  input  clk,
  input  rst,
  input  [31:0] Dwrite,
  input  [4:0] Awrite,
  input  [4:0] Aread0,
  input  [4:0] Aread1,
  output [31:0] Dread0,
  output [31:0] Dread1,
  output [31:0] R1,
  output [31:0] R2,
  output [31:0] R3,
  output [31:0] R4,
  output [31:0] R5,
  output [31:0] R6,
  output [31:0] R7,
  output [31:0] R8,
  output [31:0] R9,
  output [31:0] R10,
  output [31:0] R11,
  output [31:0] R12,
  output [31:0] R13,
  output [31:0] R14,
  output [31:0] R15,
  output [31:0] R16,
  output [31:0] R17,
  output [31:0] R18,
  output [31:0] R19,
  output [31:0] R20,
  output [31:0] R21,
  output [31:0] R22,
  output [31:0] R23,
  output [31:0] R24,
  output [31:0] R25,
  output [31:0] R26,
  output [31:0] R27,
  output [31:0] R28,
  output [31:0] R29,
  output [31:0] R30,
  output [31:0] R31
);

  wire and_1_out, and_2_out, and_3_out, and_4_out, and_5_out, and_6_out, and_7_out, and_8_out, and_9_out,
       and_10_out, and_11_out, and_12_out, and_13_out, and_14_out, and_15_out, and_16_out, and_17_out,
       and_18_out, and_19_out, and_20_out, and_21_out, and_22_out, and_23_out, and_24_out, and_25_out,
       and_26_out, and_27_out, and_28_out, and_29_out, and_30_out, and_31_out, and_32_out, decoder_1_out0,
       decoder_1_out1, decoder_1_out2, decoder_1_out3, decoder_1_out4, decoder_1_out5, decoder_1_out6,
       decoder_1_out7, decoder_2_out0, decoder_2_out1, decoder_2_out2, decoder_2_out3, or_1_out, or_2_out,
       or_3_out, or_4_out, or_5_out, or_6_out, or_7_out, or_8_out, or_9_out, or_10_out, or_11_out, or_12_out,
       or_13_out, or_14_out, or_15_out, or_16_out, or_17_out, or_18_out, or_19_out, or_20_out, or_21_out,
       or_22_out, or_23_out, or_24_out, or_25_out, or_26_out, or_27_out, or_28_out, or_29_out, or_30_out,
       or_31_out, or_32_out, undriven_2, undriven_3, undriven_4, undriven_5;
  wire [31:0] multiplexer_1_out, multiplexer_2_out, multiplexer_3_out, multiplexer_4_out, multiplexer_5_out,
       multiplexer_6_out, multiplexer_7_out, multiplexer_8_out, multiplexer_9_out, undriven;

  Register #(.width(32)) register_1 (.D(undriven), .en(or_1_out), .clk(undriven_2));  // open: Q, clr
  or or_1 (or_1_out, undriven_5, and_1_out);
  and and_1 (and_1_out, undriven_4, undriven_3);
  Decoder #(.select(3)) decoder_1 (
    .out0(decoder_1_out0), .out1(decoder_1_out1), .out2(decoder_1_out2), .out3(decoder_1_out3),
    .out4(decoder_1_out4), .out5(decoder_1_out5), .out6(decoder_1_out6), .out7(decoder_1_out7),
    .sel(Awrite[4:2]));  // open: en
  Decoder #(.select(2)) decoder_2 (
    .out0(decoder_2_out0), .out1(decoder_2_out1), .out2(decoder_2_out2), .out3(decoder_2_out3),
    .sel(Awrite[1:0]));  // open: en
  Multiplexer #(.width(32)) multiplexer_1 (.in0(Dwrite), .in1({32{1'b0}}), .out(multiplexer_1_out), .sel(rst));
  and and_2 (and_2_out, decoder_2_out0, decoder_1_out1);
  and and_3 (and_3_out, decoder_2_out0, decoder_1_out2);
  and and_4 (and_4_out, decoder_2_out0, decoder_1_out3);
  and and_5 (and_5_out, decoder_2_out0, decoder_1_out4);
  and and_6 (and_6_out, decoder_2_out0, decoder_1_out5);
  and and_7 (and_7_out, decoder_2_out0, decoder_1_out6);
  and and_8 (and_8_out, decoder_2_out0, decoder_1_out7);
  Register #(.width(32)) register_2 (.D(multiplexer_1_out), .en(or_2_out), .clk(clk), .Q(R4));  // open: clr
  or or_2 (or_2_out, rst, and_2_out);
  Register #(.width(32)) register_3 (.D(multiplexer_1_out), .en(or_3_out), .clk(clk), .Q(R8));  // open: clr
  or or_3 (or_3_out, rst, and_3_out);
  Register #(.width(32)) register_4 (.D(multiplexer_1_out), .en(or_4_out), .clk(clk), .Q(R12));  // open: clr
  or or_4 (or_4_out, rst, and_4_out);
  Register #(.width(32)) register_5 (.D(multiplexer_1_out), .en(or_5_out), .clk(clk), .Q(R16));  // open: clr
  or or_5 (or_5_out, rst, and_5_out);
  Register #(.width(32)) register_6 (.D(multiplexer_1_out), .en(or_6_out), .clk(clk), .Q(R20));  // open: clr
  or or_6 (or_6_out, rst, and_6_out);
  Register #(.width(32)) register_7 (.D(multiplexer_1_out), .en(or_7_out), .clk(clk), .Q(R24));  // open: clr
  or or_7 (or_7_out, rst, and_7_out);
  Register #(.width(32)) register_8 (.D(multiplexer_1_out), .en(or_8_out), .clk(clk), .Q(R28));  // open: clr
  or or_8 (or_8_out, rst, and_8_out);
  Multiplexer #(.select(3), .width(32)) multiplexer_2 (
    .in0({32{1'b0}}), .in1(R4), .in2(R8), .in3(R12), .in4(R16), .in5(R20), .in6(R24), .in7(R28),
    .out(multiplexer_2_out), .sel(Aread0[4:2]));
  Multiplexer #(.select(3), .width(32)) multiplexer_3 (
    .in0({32{1'b0}}), .in1(R4), .in2(R8), .in3(R12), .in4(R16), .in5(R20), .in6(R24), .in7(R28),
    .out(multiplexer_3_out), .sel(Aread1[4:2]));
  and and_9 (and_9_out, decoder_2_out1, decoder_1_out0);
  and and_10 (and_10_out, decoder_2_out1, decoder_1_out1);
  and and_11 (and_11_out, decoder_2_out1, decoder_1_out2);
  and and_12 (and_12_out, decoder_2_out1, decoder_1_out3);
  and and_13 (and_13_out, decoder_2_out1, decoder_1_out4);
  and and_14 (and_14_out, decoder_2_out1, decoder_1_out5);
  and and_15 (and_15_out, decoder_2_out1, decoder_1_out6);
  and and_16 (and_16_out, decoder_2_out1, decoder_1_out7);
  Register #(.width(32)) register_9 (.D(multiplexer_1_out), .en(or_9_out), .clk(clk), .Q(R1));  // open: clr
  or or_9 (or_9_out, rst, and_9_out);
  Register #(.width(32)) register_10 (.D(multiplexer_1_out), .en(or_10_out), .clk(clk), .Q(R5));  // open: clr
  or or_10 (or_10_out, rst, and_10_out);
  Register #(.width(32)) register_11 (.D(multiplexer_1_out), .en(or_11_out), .clk(clk), .Q(R9));  // open: clr
  or or_11 (or_11_out, rst, and_11_out);
  Register #(.width(32)) register_12 (.D(multiplexer_1_out), .en(or_12_out), .clk(clk), .Q(R13));  // open: clr
  or or_12 (or_12_out, rst, and_12_out);
  Register #(.width(32)) register_13 (.D(multiplexer_1_out), .en(or_13_out), .clk(clk), .Q(R17));  // open: clr
  or or_13 (or_13_out, rst, and_13_out);
  Register #(.width(32)) register_14 (.D(multiplexer_1_out), .en(or_14_out), .clk(clk), .Q(R21));  // open: clr
  or or_14 (or_14_out, rst, and_14_out);
  Register #(.width(32)) register_15 (.D(multiplexer_1_out), .en(or_15_out), .clk(clk), .Q(R25));  // open: clr
  or or_15 (or_15_out, rst, and_15_out);
  Register #(.width(32)) register_16 (.D(multiplexer_1_out), .en(or_16_out), .clk(clk), .Q(R29));  // open: clr
  or or_16 (or_16_out, rst, and_16_out);
  Multiplexer #(.select(3), .width(32)) multiplexer_4 (
    .in0(R1), .in1(R5), .in2(R9), .in3(R13), .in4(R17), .in5(R21), .in6(R25), .in7(R29),
    .out(multiplexer_4_out), .sel(Aread0[4:2]));
  Multiplexer #(.select(3), .width(32)) multiplexer_5 (
    .in0(R1), .in1(R5), .in2(R9), .in3(R13), .in4(R17), .in5(R21), .in6(R25), .in7(R29),
    .out(multiplexer_5_out), .sel(Aread1[4:2]));
  Register #(.width(32)) register_17 (.D(multiplexer_1_out), .en(or_17_out), .clk(clk), .Q(R2));  // open: clr
  or or_17 (or_17_out, rst, and_17_out);
  and and_17 (and_17_out, decoder_2_out2, decoder_1_out0);
  Register #(.width(32)) register_18 (.D(multiplexer_1_out), .en(or_18_out), .clk(clk), .Q(R6));  // open: clr
  or or_18 (or_18_out, rst, and_18_out);
  and and_18 (and_18_out, decoder_2_out2, decoder_1_out1);
  Register #(.width(32)) register_19 (.D(multiplexer_1_out), .en(or_19_out), .clk(clk), .Q(R10));  // open: clr
  or or_19 (or_19_out, rst, and_19_out);
  and and_19 (and_19_out, decoder_2_out2, decoder_1_out2);
  Register #(.width(32)) register_20 (.D(multiplexer_1_out), .en(or_20_out), .clk(clk), .Q(R14));  // open: clr
  or or_20 (or_20_out, rst, and_20_out);
  and and_20 (and_20_out, decoder_2_out2, decoder_1_out3);
  Register #(.width(32)) register_21 (.D(multiplexer_1_out), .en(or_21_out), .clk(clk), .Q(R18));  // open: clr
  or or_21 (or_21_out, rst, and_21_out);
  and and_21 (and_21_out, decoder_2_out2, decoder_1_out4);
  Register #(.width(32)) register_22 (.D(multiplexer_1_out), .en(or_22_out), .clk(clk), .Q(R22));  // open: clr
  or or_22 (or_22_out, rst, and_22_out);
  and and_22 (and_22_out, decoder_2_out2, decoder_1_out5);
  Register #(.width(32)) register_23 (.D(multiplexer_1_out), .en(or_23_out), .clk(clk), .Q(R26));  // open: clr
  or or_23 (or_23_out, rst, and_23_out);
  and and_23 (and_23_out, decoder_2_out2, decoder_1_out6);
  Register #(.width(32)) register_24 (.D(multiplexer_1_out), .en(or_24_out), .clk(clk), .Q(R30));  // open: clr
  or or_24 (or_24_out, rst, and_24_out);
  and and_24 (and_24_out, decoder_2_out2, decoder_1_out7);
  Multiplexer #(.select(3), .width(32)) multiplexer_6 (
    .in0(R2), .in1(R6), .in2(R10), .in3(R14), .in4(R18), .in5(R22), .in6(R26), .in7(R30),
    .out(multiplexer_6_out), .sel(Aread0[4:2]));
  Multiplexer #(.select(3), .width(32)) multiplexer_7 (
    .in0(R2), .in1(R6), .in2(R10), .in3(R14), .in4(R18), .in5(R22), .in6(R26), .in7(R30),
    .out(multiplexer_7_out), .sel(Aread1[4:2]));
  Register #(.width(32)) register_25 (.D(multiplexer_1_out), .en(or_25_out), .clk(clk), .Q(R3));  // open: clr
  or or_25 (or_25_out, rst, and_25_out);
  and and_25 (and_25_out, decoder_2_out3, decoder_1_out0);
  Register #(.width(32)) register_26 (.D(multiplexer_1_out), .en(or_26_out), .clk(clk), .Q(R7));  // open: clr
  or or_26 (or_26_out, rst, and_26_out);
  and and_26 (and_26_out, decoder_2_out3, decoder_1_out1);
  Register #(.width(32)) register_27 (.D(multiplexer_1_out), .en(or_27_out), .clk(clk), .Q(R11));  // open: clr
  or or_27 (or_27_out, rst, and_27_out);
  and and_27 (and_27_out, decoder_2_out3, decoder_1_out2);
  Register #(.width(32)) register_28 (.D(multiplexer_1_out), .en(or_28_out), .clk(clk), .Q(R15));  // open: clr
  or or_28 (or_28_out, rst, and_28_out);
  and and_28 (and_28_out, decoder_2_out3, decoder_1_out3);
  Register #(.width(32)) register_29 (.D(multiplexer_1_out), .en(or_29_out), .clk(clk), .Q(R19));  // open: clr
  or or_29 (or_29_out, rst, and_29_out);
  and and_29 (and_29_out, decoder_2_out3, decoder_1_out4);
  Register #(.width(32)) register_30 (.D(multiplexer_1_out), .en(or_30_out), .clk(clk), .Q(R23));  // open: clr
  or or_30 (or_30_out, rst, and_30_out);
  and and_30 (and_30_out, decoder_2_out3, decoder_1_out5);
  Register #(.width(32)) register_31 (.D(multiplexer_1_out), .en(or_31_out), .clk(clk), .Q(R27));  // open: clr
  or or_31 (or_31_out, rst, and_31_out);
  and and_31 (and_31_out, decoder_2_out3, decoder_1_out6);
  Register #(.width(32)) register_32 (.D(multiplexer_1_out), .en(or_32_out), .clk(clk), .Q(R31));  // open: clr
  or or_32 (or_32_out, rst, and_32_out);
  and and_32 (and_32_out, decoder_2_out3, decoder_1_out7);
  Multiplexer #(.select(3), .width(32)) multiplexer_8 (
    .in0(R3), .in1(R7), .in2(R11), .in3(R15), .in4(R19), .in5(R23), .in6(R27), .in7(R31),
    .out(multiplexer_8_out), .sel(Aread0[4:2]));
  Multiplexer #(.select(3), .width(32)) multiplexer_9 (
    .in0(R3), .in1(R7), .in2(R11), .in3(R15), .in4(R19), .in5(R23), .in6(R27), .in7(R31),
    .out(multiplexer_9_out), .sel(Aread1[4:2]));
  Multiplexer #(.select(2), .width(32)) multiplexer_10 (
    .in0(multiplexer_2_out), .in1(multiplexer_4_out), .in2(multiplexer_6_out), .in3(multiplexer_8_out),
    .out(Dread0), .sel(Aread0[1:0]));
  Multiplexer #(.select(2), .width(32)) multiplexer_11 (
    .in0(multiplexer_3_out), .in1(multiplexer_5_out), .in2(multiplexer_7_out), .in3(multiplexer_9_out),
    .out(Dread1), .sel(Aread1[1:0]));

  // Notes on the sheet:
  //   Field Template
endmodule

module shift (
  input  [31:0] q,
  input  [31:0] a,
  output [31:0] new_q,
  output [31:0] new_a
);


  assign new_a = {a[30:0], q[31]};
  assign new_q = {q[30:0], 1'b0};
endmodule

module divison (
  input  [31:0] divisor,
  input  [31:0] dividend,
  input  start,
  input  clk,
  input  rst,
  output [31:0] quotient,
  output [31:0] remainder,
  output done
);

  wire comparator_1_eq, comparator_2_gt, not_1_out, not_2_out, or_1_out, or_3_out, or_4_out;
  wire [6:0] counter_1_q, multiplexer_1_out;
  wire [31:0] b_q, D_a, D_q, multiplexer_2_out, multiplexer_5_out, or_2_out, shift_1_new_a, shift_1_new_q,
       subtractor_1_out;

  Multiplexer #(.width(7)) multiplexer_1 (.in0({7{1'b0}}), .in1(7'b0100000), .out(multiplexer_1_out), .sel(start));
  Counter #(.max('h7f), .width(7)) counter_1 (
    .load(or_1_out), .up(1'b0), .clk(clk), .D(multiplexer_1_out), .Q(counter_1_q));  // open: clr, count, carry
  or or_1 (or_1_out, start, comparator_1_eq);
  assign or_2_out = shift_1_new_q | 32'h1;  // OR_Gate or_2, 32 bits wide
  Subtractor #(.width(32)) subtractor_1 (.a(shift_1_new_a), .b(b_q), .out(subtractor_1_out));  // open: bin, bout
  Register #(.width(32)) q (.D(multiplexer_2_out), .en(or_3_out), .clk(clk), .Q(quotient), .clr(rst));
  Multiplexer #(.width(32)) multiplexer_2 (.in0(D_q), .in1(dividend), .out(multiplexer_2_out), .sel(start));
  Multiplexer #(.width(32)) multiplexer_3 (.in0(shift_1_new_q), .in1(or_2_out), .out(D_q), .sel(not_2_out));
  Multiplexer #(.width(32)) multiplexer_4 (.in0(shift_1_new_a), .in1(subtractor_1_out), .out(D_a), .sel(not_2_out));
  shift shift_1 (.q(quotient), .a(remainder), .new_q(shift_1_new_q), .new_a(shift_1_new_a));
  Register #(.width(32)) a (.D(multiplexer_5_out), .en(or_3_out), .clk(clk), .Q(remainder), .clr(rst));
  Multiplexer #(.width(32)) multiplexer_5 (.in0(D_a), .in1({32{1'b0}}), .out(multiplexer_5_out), .sel(start));
  Comparator #(.mode("unsigned"), .width(7)) comparator_1 (
    .a({7{1'b0}}), .b(counter_1_q), .eq(comparator_1_eq));  // open: gt, lt
  or or_3 (or_3_out, start, not_1_out);
  not not_1 (not_1_out, comparator_1_eq);
  Comparator #(.mode("unsigned"), .width(32)) comparator_2 (
    .a(b_q), .b(shift_1_new_a), .gt(comparator_2_gt));  // open: eq, lt
  Register #(.width(32)) b (.D(divisor), .en(start), .clk(clk), .Q(b_q), .clr(rst));
  D_Flip_Flop d_ff_1 (.D(or_4_out), .clk(clk), .Q(done), .reset(start));  // open: Qn, preset
  or or_4 (or_4_out, done, comparator_1_eq);
  not not_2 (not_2_out, comparator_2_gt);
endmodule

module ALU (
  input  [31:0] b,
  input  [31:0] a,
  input  [3:0] aluop,
  input  output_inverted,
  input  output_inc,
  input  clk,
  input  rst,
  output [31:0] res_high,
  output done,
  output [31:0] res_low
);

  wire adder_2_cout, and_1_out, and_3_out, comparator_1_eq, comparator_2_eq, done_2, done_3, start,
       Sub_Calculator_carry_out;
  wire [0:0] High_Sum;
  wire [31:0] adder_1_out, adder_2_out, and_2_out, CLO_output, CLZ_output, Div_Calculator_quotient,
       Div_Calculator_remainder, High_shift_left, High_shift_right, High_Sub, left_shift_Calculator_res_low,
       multiplexer_1_out, multiplexer_2_out, multiplexer_3_out, multiplexer_4_out, multiplexer_5_out,
       multiply_calculator_res_low, not_1_out, not_2_out, not_3_out, not_4_out, or_1_out, res_high_t,
       right_shift_Calculator_res_low, rotation_Calculator_res_low, Sub, Sum, xor_1_out;

  Comparator #(.width(4)) comparator_1 (.a(aluop), .b(4'b0011), .eq(comparator_1_eq));  // open: gt, lt
  and and_1 (and_1_out, start, comparator_1_eq);
  handle_start change_a_or_b (.a(a), .b(b), .clk(clk), .rst(rst), .aluop(aluop), .start(start));
  Comparator #(.width(4)) comparator_2 (.a(aluop), .b(4'b0010), .eq(comparator_2_eq));  // open: gt, lt
  divison Div_Calculator (
    .divisor(b), .dividend(a), .start(and_1_out), .clk(clk), .rst(rst), .quotient(Div_Calculator_quotient),
    .remainder(Div_Calculator_remainder), .done(done_3));
  assign and_2_out = a & b;  // AND_Gate and_2, 32 bits wide
  assign or_1_out = a | b;  // OR_Gate or_1, 32 bits wide
  assign xor_1_out = a ^ b;  // XOR_Gate xor_1, 32 bits wide
  Multiplexer #(.select(4), .width(32)) multiplexer_1 (
    .in0({{31{1'b0}}, High_Sum[0]}), .in1(High_Sub), .in2(res_high_t), .in3(Div_Calculator_remainder),
    .in4({32{1'b0}}), .in5({32{1'b0}}), .in6({32{1'b0}}), .in7({32{1'b0}}), .in8({32{1'b0}}),
    .in9(High_shift_left), .in10(High_shift_right), .in11(High_shift_right), .in12({32{1'b0}}),
    .out(multiplexer_1_out), .sel(aluop));  // open: in13, in14, in15
  Multiplexer #(.select(4), .width(32)) multiplexer_2 (
    .in0(Sum), .in1(Sub), .in2(multiply_calculator_res_low), .in3(Div_Calculator_quotient), .in4(and_2_out),
    .in5(or_1_out), .in6(xor_1_out), .in7(CLO_output), .in8(CLZ_output), .in9(left_shift_Calculator_res_low),
    .in10(right_shift_Calculator_res_low), .in11(right_shift_Calculator_res_low),
    .in12(rotation_Calculator_res_low), .out(multiplexer_2_out), .sel(aluop));  // open: in13, in14, in15
  and and_3 (and_3_out, start, comparator_2_eq);
  assign not_1_out = ~b;  // NOT_Gate not_1, 32 bits wide
  assign not_2_out = ~a;  // NOT_Gate not_2, 32 bits wide
  assign not_3_out = ~multiplexer_1_out;  // NOT_Gate not_3, 32 bits wide
  assign not_4_out = ~multiplexer_2_out;  // NOT_Gate not_4, 32 bits wide
  Multiplexer #(.width(32)) multiplexer_3 (
    .in0(multiplexer_1_out), .in1(not_3_out), .out(multiplexer_3_out), .sel(output_inverted));
  Carry_Select_Adder Sum_Calculator (.a(a), .b(b), .Carry_in(1'b0), .Carry_out(High_Sum[0]), .Sum(Sum));
  Carry_Select_Adder Sub_Calculator (
    .a(a), .b(not_1_out), .Carry_in(1'b1), .Carry_out(Sub_Calculator_carry_out), .Sum(Sub));
  CLO_circuit CLO_Calculator (.a(a), .count_CLO(CLO_output));
  CLO_circuit CLZ_Calculator (.a(not_2_out), .count_CLO(CLZ_output));
  left_shift left_shift_Calculator (.a(a), .b(b), .res_low(left_shift_Calculator_res_low), .res_high(High_shift_left));
  right_shift right_shift_Calculator (
    .aluop(aluop), .a(a), .b(b), .res_low(right_shift_Calculator_res_low), .res_high(High_shift_right));
  rotate rotation_Calculator (.a(a), .b(b), .res_low(rotation_Calculator_res_low));
  multiply multiply_calculator (
    .a(a), .b(b), .start(and_3_out), .clk(clk), .rst(rst), .res_high(res_high_t),
    .res_low(multiply_calculator_res_low), .done(done_2));
  Multiplexer #(.width(32)) multiplexer_4 (
    .in0(multiplexer_2_out), .in1(not_4_out), .out(multiplexer_4_out), .sel(output_inverted));
  Multiplexer #(.width(32)) multiplexer_5 (.in0({32{1'b0}}), .in1(32'h1), .out(multiplexer_5_out), .sel(output_inc));
  Adder #(.width(32)) adder_1 (
    .a(multiplexer_3_out), .b({32{1'b0}}), .out(adder_1_out), .cin(adder_2_cout));  // open: cout
  Multiplexer #(.width(32)) multiplexer_6 (
    .in0({32{1'b1}}), .in1({32{1'b0}}), .out(High_Sub), .sel(Sub_Calculator_carry_out));
  Adder #(.width(32)) adder_2 (
    .a(multiplexer_4_out), .b(multiplexer_5_out), .out(adder_2_out), .cout(adder_2_cout));  // open: cin
  Multiplexer #(.width(32)) multiplexer_7 (.in0(adder_1_out), .in1({32{1'b0}}), .out(res_high), .sel(rst));
  Multiplexer #(.width(32)) multiplexer_8 (.in0(adder_2_out), .in1({32{1'b0}}), .out(res_low), .sel(rst));
  Multiplexer #(.select(4)) multiplexer_9 (
    .in0(1'b1), .in1(1'b1), .in2(done_2), .in3(done_3), .in4(1'b1), .in5(1'b1), .in6(1'b1), .in7(1'b1),
    .in8(1'b1), .in9(1'b1), .in10(1'b1), .in11(1'b1), .in12(1'b1), .out(done), .sel(aluop));  // open: in13, in14, in15

  // Other names for the same wires on the sheet: increase = output_inc; invert = output_inverted; reset = rst
endmodule

module sign_extended (
  input  sign,
  input  [31:0] a,
  output [63:0] a_extend
);

  wire [31:0] multiplexer_1_out;

  Multiplexer #(.width(32)) multiplexer_1 (.in0({32{1'b0}}), .in1({32{1'b1}}), .out(multiplexer_1_out), .sel(a[31]));
  Multiplexer #(.width(32)) multiplexer_2 (
    .in0({32{1'b0}}), .in1(multiplexer_1_out), .out(a_extend[63:32]), .sel(sign));

  assign a_extend[31:0] = a;
endmodule

module left_shifter_1 (
  input  [63:0] a,
  output [63:0] a_1_left_shift
);


  assign a_1_left_shift = {a[62:0], 1'b0};
endmodule

module right_shifter_1 (
  input  [63:0] a,
  output [63:0] a_1_right_shift
);


  assign a_1_right_shift = {{2{a[63]}}, a[62:1]};
endmodule

module CLO_circuit (
  input  [31:0] a,
  output [31:0] count_CLO
);

  wire and_1_out, and_2_out, and_3_out, and_4_out, and_5_out, and_6_out, and_7_out, and_8_out, and_9_out,
       and_10_out, and_11_out, and_12_out, and_13_out, and_14_out, and_15_out, and_16_out, and_17_out,
       and_18_out, and_19_out, and_20_out, and_21_out, and_22_out, and_23_out, and_24_out, and_25_out,
       and_26_out, and_27_out, and_28_out, and_29_out, and_30_out, and_31_out, and_32_out;
  wire [5:0] multiplexer_1_out, multiplexer_3_out, multiplexer_4_out, multiplexer_5_out, multiplexer_6_out,
       multiplexer_7_out, multiplexer_8_out, multiplexer_9_out, multiplexer_10_out, multiplexer_11_out,
       multiplexer_12_out, multiplexer_13_out, multiplexer_14_out, multiplexer_15_out, multiplexer_16_out,
       multiplexer_17_out, multiplexer_18_out, multiplexer_19_out, multiplexer_20_out, multiplexer_21_out,
       multiplexer_22_out, multiplexer_23_out, multiplexer_24_out, multiplexer_25_out, multiplexer_26_out,
       multiplexer_27_out, multiplexer_28_out, multiplexer_29_out, multiplexer_30_out, multiplexer_31_out,
       multiplexer_32_out;

  and and_1 (and_1_out, a[31], 1'b1);
  and and_2 (and_2_out, a[30], and_1_out);
  and and_3 (and_3_out, a[29], and_2_out);
  and and_4 (and_4_out, a[28], and_3_out);
  and and_5 (and_5_out, a[27], and_4_out);
  and and_6 (and_6_out, a[26], and_5_out);
  and and_7 (and_7_out, a[25], and_6_out);
  and and_8 (and_8_out, a[24], and_7_out);
  and and_9 (and_9_out, a[23], and_8_out);
  and and_10 (and_10_out, a[22], and_9_out);
  and and_11 (and_11_out, a[21], and_10_out);
  and and_12 (and_12_out, a[20], and_11_out);
  and and_13 (and_13_out, a[19], and_12_out);
  and and_14 (and_14_out, a[18], and_13_out);
  and and_15 (and_15_out, a[17], and_14_out);
  and and_16 (and_16_out, a[16], and_15_out);
  and and_17 (and_17_out, a[15], and_16_out);
  and and_18 (and_18_out, a[14], and_17_out);
  and and_19 (and_19_out, a[13], and_18_out);
  and and_20 (and_20_out, a[12], and_19_out);
  and and_21 (and_21_out, a[11], and_20_out);
  and and_22 (and_22_out, a[10], and_21_out);
  and and_23 (and_23_out, a[9], and_22_out);
  and and_24 (and_24_out, a[8], and_23_out);
  and and_25 (and_25_out, a[7], and_24_out);
  and and_26 (and_26_out, a[6], and_25_out);
  and and_27 (and_27_out, a[5], and_26_out);
  and and_28 (and_28_out, a[4], and_27_out);
  and and_29 (and_29_out, a[3], and_28_out);
  and and_30 (and_30_out, a[2], and_29_out);
  and and_31 (and_31_out, a[1], and_30_out);
  and and_32 (and_32_out, a[0], and_31_out);
  Multiplexer #(.width(6)) multiplexer_1 (.in0({6{1'b0}}), .in1(6'b000001), .out(multiplexer_1_out), .sel(and_1_out));
  Multiplexer #(.width(6)) multiplexer_2 (
    .in0(multiplexer_1_out), .in1(multiplexer_3_out), .out(count_CLO[5:0]), .sel(and_2_out));
  Multiplexer #(.width(6)) multiplexer_3 (
    .in0(6'b000010), .in1(multiplexer_4_out), .out(multiplexer_3_out), .sel(and_3_out));
  Multiplexer #(.width(6)) multiplexer_4 (
    .in0(6'b000011), .in1(multiplexer_5_out), .out(multiplexer_4_out), .sel(and_4_out));
  Multiplexer #(.width(6)) multiplexer_5 (
    .in0(6'b000100), .in1(multiplexer_6_out), .out(multiplexer_5_out), .sel(and_5_out));
  Multiplexer #(.width(6)) multiplexer_6 (
    .in0(6'b000101), .in1(multiplexer_7_out), .out(multiplexer_6_out), .sel(and_6_out));
  Multiplexer #(.width(6)) multiplexer_7 (
    .in0(6'b000110), .in1(multiplexer_8_out), .out(multiplexer_7_out), .sel(and_7_out));
  Multiplexer #(.width(6)) multiplexer_8 (
    .in0(6'b000111), .in1(multiplexer_9_out), .out(multiplexer_8_out), .sel(and_8_out));
  Multiplexer #(.width(6)) multiplexer_9 (
    .in0(6'b001000), .in1(multiplexer_10_out), .out(multiplexer_9_out), .sel(and_9_out));
  Multiplexer #(.width(6)) multiplexer_10 (
    .in0(6'b001001), .in1(multiplexer_11_out), .out(multiplexer_10_out), .sel(and_10_out));
  Multiplexer #(.width(6)) multiplexer_11 (
    .in0(6'b001010), .in1(multiplexer_12_out), .out(multiplexer_11_out), .sel(and_11_out));
  Multiplexer #(.width(6)) multiplexer_12 (
    .in0(6'b001011), .in1(multiplexer_13_out), .out(multiplexer_12_out), .sel(and_12_out));
  Multiplexer #(.width(6)) multiplexer_13 (
    .in0(6'b001100), .in1(multiplexer_14_out), .out(multiplexer_13_out), .sel(and_13_out));
  Multiplexer #(.width(6)) multiplexer_14 (
    .in0(6'b001101), .in1(multiplexer_15_out), .out(multiplexer_14_out), .sel(and_14_out));
  Multiplexer #(.width(6)) multiplexer_15 (
    .in0(6'b001110), .in1(multiplexer_16_out), .out(multiplexer_15_out), .sel(and_15_out));
  Multiplexer #(.width(6)) multiplexer_16 (
    .in0(6'b001111), .in1(multiplexer_17_out), .out(multiplexer_16_out), .sel(and_16_out));
  Multiplexer #(.width(6)) multiplexer_17 (
    .in0(6'b010000), .in1(multiplexer_18_out), .out(multiplexer_17_out), .sel(and_17_out));
  Multiplexer #(.width(6)) multiplexer_18 (
    .in0(6'b010001), .in1(multiplexer_19_out), .out(multiplexer_18_out), .sel(and_18_out));
  Multiplexer #(.width(6)) multiplexer_19 (
    .in0(6'b010010), .in1(multiplexer_20_out), .out(multiplexer_19_out), .sel(and_19_out));
  Multiplexer #(.width(6)) multiplexer_20 (
    .in0(6'b010011), .in1(multiplexer_21_out), .out(multiplexer_20_out), .sel(and_20_out));
  Multiplexer #(.width(6)) multiplexer_21 (
    .in0(6'b010100), .in1(multiplexer_22_out), .out(multiplexer_21_out), .sel(and_21_out));
  Multiplexer #(.width(6)) multiplexer_22 (
    .in0(6'b010101), .in1(multiplexer_23_out), .out(multiplexer_22_out), .sel(and_22_out));
  Multiplexer #(.width(6)) multiplexer_23 (
    .in0(6'b010110), .in1(multiplexer_24_out), .out(multiplexer_23_out), .sel(and_23_out));
  Multiplexer #(.width(6)) multiplexer_24 (
    .in0(6'b010111), .in1(multiplexer_25_out), .out(multiplexer_24_out), .sel(and_24_out));
  Multiplexer #(.width(6)) multiplexer_25 (
    .in0(6'b011000), .in1(multiplexer_26_out), .out(multiplexer_25_out), .sel(and_25_out));
  Multiplexer #(.width(6)) multiplexer_26 (
    .in0(6'b011001), .in1(multiplexer_27_out), .out(multiplexer_26_out), .sel(and_26_out));
  Multiplexer #(.width(6)) multiplexer_27 (
    .in0(6'b011010), .in1(multiplexer_28_out), .out(multiplexer_27_out), .sel(and_27_out));
  Multiplexer #(.width(6)) multiplexer_28 (
    .in0(6'b011011), .in1(multiplexer_29_out), .out(multiplexer_28_out), .sel(and_28_out));
  Multiplexer #(.width(6)) multiplexer_29 (
    .in0(6'b011100), .in1(multiplexer_30_out), .out(multiplexer_29_out), .sel(and_29_out));
  Multiplexer #(.width(6)) multiplexer_30 (
    .in0(6'b011101), .in1(multiplexer_31_out), .out(multiplexer_30_out), .sel(and_30_out));
  Multiplexer #(.width(6)) multiplexer_31 (
    .in0(6'b011110), .in1(multiplexer_32_out), .out(multiplexer_31_out), .sel(and_31_out));
  Multiplexer #(.width(6)) multiplexer_32 (
    .in0(6'b011111), .in1(6'b100000), .out(multiplexer_32_out), .sel(and_32_out));

  assign count_CLO[31:6] = {26{1'b0}};
endmodule

module Carry_Select_Adder (
  input  [31:0] a,
  input  [31:0] b,
  input  Carry_in,
  output Carry_out,
  output [31:0] Sum
);

  wire adder_1_cout, adder_2_cout, adder_3_cout, adder_4_cout, adder_5_cout, adder_6_cout, adder_7_cout,
       multiplexer_5_out, multiplexer_6_out;
  wire [7:0] adder_1_out, adder_2_out, adder_3_out, adder_5_out, adder_6_out, adder_7_out;

  Adder adder_1 (.a(a[31:24]), .b(b[31:24]), .out(adder_1_out), .cin(1'b0), .cout(adder_1_cout));
  Adder adder_2 (.a(a[23:16]), .b(b[23:16]), .out(adder_2_out), .cin(1'b0), .cout(adder_2_cout));
  Adder adder_3 (.a(a[15:8]), .b(b[15:8]), .out(adder_3_out), .cin(1'b0), .cout(adder_3_cout));
  Adder adder_4 (.a(a[7:0]), .b(b[7:0]), .out(Sum[7:0]), .cin(Carry_in), .cout(adder_4_cout));
  Multiplexer #(.width(8)) multiplexer_1 (
    .in0(adder_1_out), .in1(adder_5_out), .out(Sum[31:24]), .sel(multiplexer_5_out));
  Multiplexer #(.width(8)) multiplexer_2 (
    .in0(adder_2_out), .in1(adder_6_out), .out(Sum[23:16]), .sel(multiplexer_6_out));
  Multiplexer #(.width(8)) multiplexer_3 (.in0(adder_3_out), .in1(adder_7_out), .out(Sum[15:8]), .sel(adder_4_cout));
  Adder adder_5 (.a(a[31:24]), .b(b[31:24]), .out(adder_5_out), .cin(1'b1), .cout(adder_5_cout));
  Multiplexer multiplexer_4 (.in0(adder_1_cout), .in1(adder_5_cout), .out(Carry_out), .sel(multiplexer_5_out));
  Adder adder_6 (.a(a[23:16]), .b(b[23:16]), .out(adder_6_out), .cin(1'b1), .cout(adder_6_cout));
  Multiplexer multiplexer_5 (.in0(adder_2_cout), .in1(adder_6_cout), .out(multiplexer_5_out), .sel(multiplexer_6_out));
  Adder adder_7 (.a(a[15:8]), .b(b[15:8]), .out(adder_7_out), .cin(1'b1), .cout(adder_7_cout));
  Multiplexer multiplexer_6 (.in0(adder_3_cout), .in1(adder_7_cout), .out(multiplexer_6_out), .sel(adder_4_cout));
endmodule

module left_shifter_2 (
  input  [63:0] a,
  output [63:0] a_2_left_shift
);


  assign a_2_left_shift = {a[61:0], 2'b00};
endmodule

module left_shifter_4 (
  input  [63:0] a,
  output [63:0] a_4_left_shift
);


  assign a_4_left_shift = {a[59:0], 4'b0000};
endmodule

module left_shifter_8 (
  input  [63:0] a,
  output [63:0] a_8_left_shift
);


  assign a_8_left_shift = {a[55:0], {8{1'b0}}};
endmodule

module left_shifter_16 (
  input  [63:0] a,
  output [63:0] a_16_left_shift
);


  assign a_16_left_shift = {a[47:0], {16{1'b0}}};
endmodule

module right_shifter_2 (
  input  [63:0] a,
  output [63:0] a_2_right_shift
);


  assign a_2_right_shift = {a[63:62], a[63:2]};
endmodule

module right_shifter_4 (
  input  [63:0] a,
  output [63:0] a_4_right_shift
);


  assign a_4_right_shift = {a[63:60], a[63:4]};
endmodule

module right_shifter_8 (
  input  [63:0] a,
  output [63:0] a_8_right_shift
);


  assign a_8_right_shift = {a[63:56], a[63:8]};
endmodule

module right_shifter_16 (
  input  [63:0] a,
  output [63:0] a_16_right_shift
);


  assign a_16_right_shift = {a[63:48], a[63:16]};
endmodule

module left_shift (
  input  [31:0] a,
  input  [31:0] b,
  output [31:0] res_low,
  output [31:0] res_high
);

  wire [63:0] left_shift_2_a_2_left_shift, left_shift_4_a_4_left_shift, left_shift_8_a_8_left_shift,
       left_Shift_16_a_16_left_shift, left_shifte_1_a_1_left_shift, multiplexer_1_out, multiplexer_2_out,
       multiplexer_3_out, multiplexer_4_out, shign_extended_a_extend;

  sign_extended shign_extended (.sign(1'b0), .a(a), .a_extend(shign_extended_a_extend));
  left_shifter_1 left_shifte_1 (.a(shign_extended_a_extend), .a_1_left_shift(left_shifte_1_a_1_left_shift));
  Multiplexer #(.width(64)) multiplexer_1 (
    .in0(shign_extended_a_extend), .in1(left_shifte_1_a_1_left_shift), .out(multiplexer_1_out), .sel(b[0]));
  left_shifter_2 left_shift_2 (.a(multiplexer_1_out), .a_2_left_shift(left_shift_2_a_2_left_shift));
  Multiplexer #(.width(64)) multiplexer_2 (
    .in0(multiplexer_1_out), .in1(left_shift_2_a_2_left_shift), .out(multiplexer_2_out), .sel(b[1]));
  Multiplexer #(.width(64)) multiplexer_3 (
    .in0(multiplexer_2_out), .in1(left_shift_4_a_4_left_shift), .out(multiplexer_3_out), .sel(b[2]));
  left_shifter_4 left_shift_4 (.a(multiplexer_2_out), .a_4_left_shift(left_shift_4_a_4_left_shift));
  Multiplexer #(.width(64)) multiplexer_4 (
    .in0(multiplexer_3_out), .in1(left_shift_8_a_8_left_shift), .out(multiplexer_4_out), .sel(b[3]));
  left_shifter_8 left_shift_8 (.a(multiplexer_3_out), .a_8_left_shift(left_shift_8_a_8_left_shift));
  Multiplexer #(.width(64)) multiplexer_5 (
    .in0(multiplexer_4_out), .in1(left_Shift_16_a_16_left_shift), .out({res_high, res_low}), .sel(b[4]));
  left_shifter_16 left_Shift_16 (.a(multiplexer_4_out), .a_16_left_shift(left_Shift_16_a_16_left_shift));
endmodule

module right_shift (
  input  [3:0] aluop,
  input  [31:0] a,
  input  [31:0] b,
  output [31:0] res_low,
  output [31:0] res_high
);

  wire comparator_1_eq, multiplexer_1_out;
  wire [63:0] multiplexer_2_out, multiplexer_3_out, multiplexer_4_out, multiplexer_5_out,
       right_shift_1_a_1_right_shift, right_shift_2_a_2_right_shift, right_shift_4_a_4_right_shift,
       right_shift_8_a_8_right_shift, right_shift_16_a_16_right_shift, shign_extend_a_extend;

  Comparator #(.width(4)) comparator_1 (.a(aluop), .b(4'b1011), .eq(comparator_1_eq));  // open: gt, lt
  Multiplexer multiplexer_1 (.in0(1'b0), .in1(1'b1), .out(multiplexer_1_out), .sel(comparator_1_eq));
  sign_extended shign_extend (.sign(multiplexer_1_out), .a(a), .a_extend(shign_extend_a_extend));
  right_shifter_1 right_shift_1 (.a(shign_extend_a_extend), .a_1_right_shift(right_shift_1_a_1_right_shift));
  Multiplexer #(.width(64)) multiplexer_2 (
    .in0(shign_extend_a_extend), .in1(right_shift_1_a_1_right_shift), .out(multiplexer_2_out), .sel(b[0]));
  right_shifter_2 right_shift_2 (.a(multiplexer_2_out), .a_2_right_shift(right_shift_2_a_2_right_shift));
  Multiplexer #(.width(64)) multiplexer_3 (
    .in0(multiplexer_2_out), .in1(right_shift_2_a_2_right_shift), .out(multiplexer_3_out), .sel(b[1]));
  right_shifter_4 right_shift_4 (.a(multiplexer_3_out), .a_4_right_shift(right_shift_4_a_4_right_shift));
  Multiplexer #(.width(64)) multiplexer_4 (
    .in0(multiplexer_3_out), .in1(right_shift_4_a_4_right_shift), .out(multiplexer_4_out), .sel(b[2]));
  right_shifter_8 right_shift_8 (.a(multiplexer_4_out), .a_8_right_shift(right_shift_8_a_8_right_shift));
  Multiplexer #(.width(64)) multiplexer_5 (
    .in0(multiplexer_4_out), .in1(right_shift_8_a_8_right_shift), .out(multiplexer_5_out), .sel(b[3]));
  right_shifter_16 right_shift_16 (.a(multiplexer_5_out), .a_16_right_shift(right_shift_16_a_16_right_shift));
  Multiplexer #(.width(64)) multiplexer_6 (
    .in0(multiplexer_5_out), .in1(right_shift_16_a_16_right_shift), .out({res_high, res_low}), .sel(b[4]));
endmodule

module right_rotate_1 (
  input  [31:0] a,
  output [31:0] a_rotate_1
);


  assign a_rotate_1 = {a[0], a[31:1]};
endmodule

module right_rotate_2 (
  input  [31:0] a,
  output [31:0] a_rotate_2
);


  assign a_rotate_2 = {a[1:0], a[31:2]};
endmodule

module right_rotate_4 (
  input  [31:0] a,
  output [31:0] a_rotate_4
);


  assign a_rotate_4 = {a[3:0], a[31:4]};
endmodule

module right_rotate_8 (
  input  [31:0] a,
  output [31:0] a_rotate_8
);


  assign a_rotate_8 = {a[7:0], a[31:8]};
endmodule

module right_rotate_16 (
  input  [31:0] a,
  output [31:0] a_rotate_16
);


  assign a_rotate_16 = {a[15:0], a[31:16]};
endmodule

module rotate (
  input  [31:0] a,
  input  [31:0] b,
  output [31:0] res_low
);

  wire [31:0] multiplexer_1_out, multiplexer_2_out, multiplexer_3_out, multiplexer_4_out,
       rotation_1_a_rotate_1, rotation_2_a_rotate_2, rotation_4_a_rotate_4, rotation_8_a_rotate_8,
       rotation_16_a_rotate_16;

  right_rotate_1 rotation_1 (.a(a), .a_rotate_1(rotation_1_a_rotate_1));
  Multiplexer #(.width(32)) multiplexer_1 (.in0(a), .in1(rotation_1_a_rotate_1), .out(multiplexer_1_out), .sel(b[0]));
  Multiplexer #(.width(32)) multiplexer_2 (
    .in0(multiplexer_1_out), .in1(rotation_2_a_rotate_2), .out(multiplexer_2_out), .sel(b[1]));
  right_rotate_2 rotation_2 (.a(multiplexer_1_out), .a_rotate_2(rotation_2_a_rotate_2));
  Multiplexer #(.width(32)) multiplexer_3 (
    .in0(multiplexer_2_out), .in1(rotation_4_a_rotate_4), .out(multiplexer_3_out), .sel(b[2]));
  right_rotate_4 rotation_4 (.a(multiplexer_2_out), .a_rotate_4(rotation_4_a_rotate_4));
  Multiplexer #(.width(32)) multiplexer_4 (
    .in0(multiplexer_3_out), .in1(rotation_8_a_rotate_8), .out(multiplexer_4_out), .sel(b[3]));
  right_rotate_8 rotation_8 (.a(multiplexer_3_out), .a_rotate_8(rotation_8_a_rotate_8));
  Multiplexer #(.width(32)) multiplexer_5 (
    .in0(multiplexer_4_out), .in1(rotation_16_a_rotate_16), .out(res_low), .sel(b[4]));
  right_rotate_16 rotation_16 (.a(multiplexer_4_out), .a_rotate_16(rotation_16_a_rotate_16));
endmodule

module Carry_Save_Adder (
  input  [31:0] a,
  input  [31:0] b,
  input  [31:0] c,
  output S0,
  output S1,
  output [31:0] new_S
);

  wire adder_33_cout;
  wire [31:0] adder_1_cout, adder_2_out;

  Adder #(.width(1)) adder_1 (.a(a[0]), .b(b[0]), .out(S0), .cin(1'b0), .cout(adder_1_cout[0]));
  Adder #(.width(1)) adder_2 (.a(a[1]), .b(b[1]), .out(adder_2_out[0]), .cin(c[0]), .cout(adder_1_cout[1]));
  Adder #(.width(1)) adder_3 (.a(a[2]), .b(b[2]), .out(adder_2_out[1]), .cin(c[1]), .cout(adder_1_cout[2]));
  Adder #(.width(1)) adder_4 (.a(a[3]), .b(b[3]), .out(adder_2_out[2]), .cin(c[2]), .cout(adder_1_cout[3]));
  Adder #(.width(1)) adder_5 (.a(a[4]), .b(b[4]), .out(adder_2_out[3]), .cin(c[3]), .cout(adder_1_cout[4]));
  Adder #(.width(1)) adder_6 (.a(a[5]), .b(b[5]), .out(adder_2_out[4]), .cin(c[4]), .cout(adder_1_cout[5]));
  Adder #(.width(1)) adder_7 (.a(a[6]), .b(b[6]), .out(adder_2_out[5]), .cin(c[5]), .cout(adder_1_cout[6]));
  Adder #(.width(1)) adder_8 (.a(a[7]), .b(b[7]), .out(adder_2_out[6]), .cin(c[6]), .cout(adder_1_cout[7]));
  Adder #(.width(1)) adder_9 (.a(a[8]), .b(b[8]), .out(adder_2_out[7]), .cin(c[7]), .cout(adder_1_cout[8]));
  Adder #(.width(1)) adder_10 (.a(a[9]), .b(b[9]), .out(adder_2_out[8]), .cin(c[8]), .cout(adder_1_cout[9]));
  Adder #(.width(1)) adder_11 (.a(a[10]), .b(b[10]), .out(adder_2_out[9]), .cin(c[9]), .cout(adder_1_cout[10]));
  Adder #(.width(1)) adder_12 (.a(a[11]), .b(b[11]), .out(adder_2_out[10]), .cin(c[10]), .cout(adder_1_cout[11]));
  Adder #(.width(1)) adder_13 (.a(a[12]), .b(b[12]), .out(adder_2_out[11]), .cin(c[11]), .cout(adder_1_cout[12]));
  Adder #(.width(1)) adder_14 (.a(a[13]), .b(b[13]), .out(adder_2_out[12]), .cin(c[12]), .cout(adder_1_cout[13]));
  Adder #(.width(1)) adder_15 (.a(a[14]), .b(b[14]), .out(adder_2_out[13]), .cin(c[13]), .cout(adder_1_cout[14]));
  Adder #(.width(1)) adder_16 (.a(a[15]), .b(b[15]), .out(adder_2_out[14]), .cin(c[14]), .cout(adder_1_cout[15]));
  Adder #(.width(1)) adder_17 (.a(a[16]), .b(b[16]), .out(adder_2_out[15]), .cin(c[15]), .cout(adder_1_cout[16]));
  Adder #(.width(1)) adder_18 (.a(a[17]), .b(b[17]), .out(adder_2_out[16]), .cin(c[16]), .cout(adder_1_cout[17]));
  Adder #(.width(1)) adder_19 (.a(a[18]), .b(b[18]), .out(adder_2_out[17]), .cin(c[17]), .cout(adder_1_cout[18]));
  Adder #(.width(1)) adder_20 (.a(a[19]), .b(b[19]), .out(adder_2_out[18]), .cin(c[18]), .cout(adder_1_cout[19]));
  Adder #(.width(1)) adder_21 (.a(a[20]), .b(b[20]), .out(adder_2_out[19]), .cin(c[19]), .cout(adder_1_cout[20]));
  Carry_Select_Adder CSA (
    .a(adder_1_cout), .b(adder_2_out), .Carry_in(1'b0), .Carry_out(new_S[31]), .Sum({new_S[30:0], S1}));
  Adder #(.width(1)) adder_22 (.a(a[21]), .b(b[21]), .out(adder_2_out[20]), .cin(c[20]), .cout(adder_1_cout[21]));
  Adder #(.width(1)) adder_23 (.a(a[22]), .b(b[22]), .out(adder_2_out[21]), .cin(c[21]), .cout(adder_1_cout[22]));
  Adder #(.width(1)) adder_24 (.a(a[23]), .b(b[23]), .out(adder_2_out[22]), .cin(c[22]), .cout(adder_1_cout[23]));
  Adder #(.width(1)) adder_25 (.a(a[24]), .b(b[24]), .out(adder_2_out[23]), .cin(c[23]), .cout(adder_1_cout[24]));
  Adder #(.width(1)) adder_26 (.a(a[25]), .b(b[25]), .out(adder_2_out[24]), .cin(c[24]), .cout(adder_1_cout[25]));
  Adder #(.width(1)) adder_27 (.a(a[26]), .b(b[26]), .out(adder_2_out[25]), .cin(c[25]), .cout(adder_1_cout[26]));
  Adder #(.width(1)) adder_28 (.a(a[27]), .b(b[27]), .out(adder_2_out[26]), .cin(c[26]), .cout(adder_1_cout[27]));
  Adder #(.width(1)) adder_29 (.a(a[28]), .b(b[28]), .out(adder_2_out[27]), .cin(c[27]), .cout(adder_1_cout[28]));
  Adder #(.width(1)) adder_30 (.a(a[29]), .b(b[29]), .out(adder_2_out[28]), .cin(c[28]), .cout(adder_1_cout[29]));
  Adder #(.width(1)) adder_31 (.a(a[30]), .b(b[30]), .out(adder_2_out[29]), .cin(c[29]), .cout(adder_1_cout[30]));
  Adder #(.width(1)) adder_32 (.a(a[31]), .b(b[31]), .out(adder_2_out[30]), .cin(c[30]), .cout(adder_1_cout[31]));
  Adder #(.width(1)) adder_33 (.a(1'b0), .b(1'b0), .out(adder_2_out[31]), .cin(c[31]), .cout(adder_33_cout));
endmodule

module multiply (
  input  [31:0] a,
  input  [31:0] b,
  input  start,
  input  clk,
  input  rst,
  output [31:0] res_high,
  output [31:0] res_low,
  output done
);

  wire comparator_1_eq, comparator_1_lt, or_1_out, or_3_out, start_or_done;
  wire [6:0] counter_1_q, multiplexer_1_out;
  wire [31:0] CSA_new_s, multiplexer_2_out, multiplexer_3_out, multiplexer_4_out, multiplexer_5_out,
       multiplexer_6_out, or_4_out, register_1_q;
  wire [31:30] CSA_s0;
  wire [63:0] right_shifter_2_1_a_2_right_shift, right_shifter_2_2_a_2_right_shift;

  Multiplexer #(.width(7)) multiplexer_1 (.in0({7{1'b0}}), .in1(7'b0010000), .out(multiplexer_1_out), .sel(start));
  Counter #(.max('h7f), .width(7)) counter_1 (
    .load(or_1_out), .up(1'b0), .clk(clk), .D(multiplexer_1_out), .Q(counter_1_q));  // open: clr, count, carry
  or or_1 (or_1_out, start, comparator_1_eq);
  right_shifter_2 right_shifter_2_1 (
    .a({{32{1'b0}}, register_1_q}), .a_2_right_shift(right_shifter_2_1_a_2_right_shift));
  Multiplexer #(.width(32)) multiplexer_2 (
    .in0(right_shifter_2_1_a_2_right_shift[31:0]), .in1(b), .out(multiplexer_2_out), .sel(start));
  Register #(.width(32)) register_1 (.D(multiplexer_2_out), .en(start_or_done), .clk(clk), .Q(register_1_q), .clr(rst));
  or or_2 (start_or_done, start, comparator_1_lt);
  Comparator #(.mode("unsigned"), .width(7)) comparator_1 (
    .a({7{1'b0}}), .b(counter_1_q), .eq(comparator_1_eq), .lt(comparator_1_lt));  // open: gt
  or or_3 (or_3_out, done, comparator_1_eq);
  Multiplexer #(.width(32)) multiplexer_3 (.in0({32{1'b0}}), .in1(a), .out(multiplexer_3_out), .sel(register_1_q[0]));
  Multiplexer #(.width(32)) multiplexer_4 (.in0({32{1'b0}}), .in1(a), .out(multiplexer_4_out), .sel(register_1_q[1]));
  D_Flip_Flop d_ff_1 (.D(or_3_out), .clk(clk), .Q(done), .reset(start));  // open: Qn, preset
  right_shifter_2 right_shifter_2_2 (.a({{32{1'b0}}, res_low}), .a_2_right_shift(right_shifter_2_2_a_2_right_shift));
  Carry_Save_Adder CSA (
    .a(res_high), .b(multiplexer_3_out), .c(multiplexer_4_out), .S0(CSA_s0[30]), .S1(CSA_s0[31]),
    .new_S(CSA_new_s));
  assign or_4_out = right_shifter_2_2_a_2_right_shift[31:0] | {CSA_s0, {30{1'b0}}};  // OR_Gate or_4, 32 bits wide
  Multiplexer #(.width(32)) multiplexer_5 (.in0(CSA_new_s), .in1({32{1'b0}}), .out(multiplexer_5_out), .sel(start));
  Multiplexer #(.width(32)) multiplexer_6 (.in0(or_4_out), .in1({32{1'b0}}), .out(multiplexer_6_out), .sel(start));
  Register #(.width(32)) register_2 (.D(multiplexer_5_out), .en(start_or_done), .clk(clk), .Q(res_high), .clr(rst));
  Register #(.width(32)) register_3 (.D(multiplexer_6_out), .en(start_or_done), .clk(clk), .Q(res_low), .clr(rst));
endmodule

module handle_start (
  input  [31:0] a,
  input  [31:0] b,
  input  clk,
  input  rst,
  input  [3:0] aluop,
  output start
);

  wire and_1_out, and_2_out, comparator_1_eq, comparator_2_eq, comparator_3_eq, comparator_4_eq,
       comparator_5_eq, not_1_out, not_2_out, not_3_out, or_1_out, or_2_out, or_3_out;
  wire [3:0] register_3_q;
  wire [31:0] register_1_q, register_2_q;

  Comparator #(.width(4)) comparator_1 (.a(aluop), .b(4'b0010), .eq(comparator_1_eq));  // open: gt, lt
  Comparator #(.width(4)) comparator_2 (.a(aluop), .b(4'b0011), .eq(comparator_2_eq));  // open: gt, lt
  Register #(.width(32)) register_1 (.D(a), .en(1'b1), .clk(clk), .Q(register_1_q), .clr(rst));
  Register #(.width(32)) register_2 (.D(b), .en(1'b1), .clk(clk), .Q(register_2_q), .clr(rst));
  or or_1 (or_1_out, comparator_1_eq, comparator_2_eq);
  Register #(.width(4)) register_3 (.D(aluop), .en(1'b1), .clk(clk), .Q(register_3_q), .clr(rst));
  Comparator #(.width(4)) comparator_3 (.a(register_3_q), .b(aluop), .eq(comparator_3_eq));  // open: gt, lt
  Comparator #(.width(32)) comparator_4 (.a(register_1_q), .b(a), .eq(comparator_4_eq));  // open: gt, lt
  Comparator #(.width(32)) comparator_5 (.a(register_2_q), .b(b), .eq(comparator_5_eq));  // open: gt, lt
  not not_1 (not_1_out, comparator_3_eq);
  not not_2 (not_2_out, comparator_4_eq);
  not not_3 (not_3_out, comparator_5_eq);
  or or_2 (or_2_out, not_2_out, not_3_out);
  and and_1 (and_1_out, or_2_out, or_1_out);
  and and_2 (and_2_out, or_1_out, not_1_out);
  or or_3 (or_3_out, and_1_out, and_2_out);
  D_Flip_Flop d_ff_1 (.D(or_3_out), .clk(clk), .Q(start), .reset(rst));  // open: Qn, preset
endmodule

module Control_Alu (
  input  [5:0] Opcode,
  input  [5:0] funct,
  output [3:0] aluop
);

  wire and_4_out, and_5_out, and_6_out, and_7_out, comparator_1_eq, comparator_2_eq, comparator_3_eq,
       comparator_4_eq, comparator_5_eq, comparator_6_eq, I_type, not_1_out, not_2_out, not_3_out, not_4_out,
       not_5_out, not_6_out, not_7_out, not_8_out, not_9_out;
  wire [3:0] multiplexer_1_out, multiplexer_2_out, multiplexer_3_out, multiplexer_4_out, multiplexer_6_out,
       or_1_out;

  Comparator #(.mode("unsigned"), .width(6)) comparator_1 (
    .a(Opcode), .b({6{1'b0}}), .eq(comparator_1_eq));  // open: gt, lt
  not not_1 (not_1_out, comparator_1_eq);
  Comparator #(.mode("unsigned"), .width(6)) comparator_2 (
    .a(Opcode), .b(6'b011100), .eq(comparator_2_eq));  // open: gt, lt
  not not_2 (not_2_out, comparator_2_eq);
  not not_3 (not_3_out, funct[5]);
  not not_4 (not_4_out, funct[5]);
  not not_5 (not_5_out, funct[1]);
  not not_6 (not_6_out, funct[0]);
  not not_7 (not_7_out, funct[1]);
  not not_8 (not_8_out, funct[2]);
  not not_9 (not_9_out, funct[0]);
  and and_1 (or_1_out[1], funct[1], funct[2]);
  and and_2 (or_1_out[2], funct[2], funct[5]);
  and and_3 (I_type, not_1_out, not_2_out);
  and and_4 (and_4_out, funct[2], not_3_out, funct[1], funct[0]);
  and and_5 (and_5_out, funct[2], not_4_out, not_5_out, not_6_out);
  and and_6 (and_6_out, funct[2], funct[5], not_7_out, funct[0]);
  and and_7 (and_7_out, funct[5], not_8_out, funct[1], not_9_out);
  not not_10 (or_1_out[3], funct[5]);
  or or_1 (or_1_out[0], and_4_out, and_5_out, and_6_out, and_7_out);
  Multiplexer #(.width(4)) multiplexer_1 (
    .in0(or_1_out), .in1(4'b0010), .out(multiplexer_1_out), .sel(comparator_3_eq));
  Comparator #(.mode("unsigned"), .width(6)) comparator_3 (
    .a(funct), .b(6'b000010), .eq(comparator_3_eq));  // open: gt, lt
  Multiplexer #(.width(4)) multiplexer_2 (
    .in0(multiplexer_1_out), .in1(4'b0011), .out(multiplexer_2_out), .sel(comparator_4_eq));
  Comparator #(.mode("unsigned"), .width(6)) comparator_4 (
    .a(6'b011010), .b(funct), .eq(comparator_4_eq));  // open: gt, lt
  Multiplexer #(.width(4)) multiplexer_3 (
    .in0(multiplexer_2_out), .in1(4'b1001), .out(multiplexer_3_out), .sel(comparator_5_eq));
  Comparator #(.mode("unsigned"), .width(6)) comparator_5 (
    .a({6{1'b0}}), .b(funct), .eq(comparator_5_eq));  // open: gt, lt
  Multiplexer #(.width(4)) multiplexer_4 (.in0(4'b0001), .in1(4'b0000), .out(multiplexer_4_out), .sel(Opcode[5]));
  Multiplexer #(.width(4)) multiplexer_5 (.in0(multiplexer_3_out), .in1(multiplexer_6_out), .out(aluop), .sel(I_type));
  Multiplexer #(.width(4)) multiplexer_6 (
    .in0(multiplexer_4_out), .in1(4'b0000), .out(multiplexer_6_out), .sel(comparator_6_eq));
  Comparator #(.mode("unsigned"), .width(6)) comparator_6 (
    .a(6'b001000), .b(Opcode), .eq(comparator_6_eq));  // open: gt, lt

  // Other names for the same wires on the sheet: op_5 = Opcode[5]
endmodule

module Control_Unit (
  input  [5:0] Opcode,
  input  [5:0] funct,
  output [3:0] aluop,
  output bne,
  output source_2,
  output jump,
  output regdst,
  output mem_to_reg,
  output mf,
  output lo_or_hi,
  output mem_write,
  output reg_write,
  output slti,
  output sll_control,
  output is_div,
  output is_jr,
  output is_jal,
  output is_mul,
  output beq
);

  wire and_1_out, comparator_1_eq, comparator_2_eq, comparator_3_eq, comparator_4_eq, comparator_6_eq,
       comparator_8_eq, comparator_11_eq, comparator_12_eq, comparator_13_eq, comparator_15_eq,
       comparator_16_eq, not_1_out, not_2_out, not_3_out, not_4_out, not_6_out, not_7_out, not_8_out,
       not_9_out, or_3_out, Rtype;

  Comparator #(.mode("unsigned"), .width(6)) comparator_1 (
    .a(6'b011100), .b(Opcode), .eq(comparator_1_eq));  // open: gt, lt
  Comparator #(.mode("unsigned"), .width(6)) comparator_2 (
    .a({6{1'b0}}), .b(Opcode), .eq(comparator_2_eq));  // open: gt, lt
  or or_1 (Rtype, comparator_1_eq, comparator_2_eq);
  not not_1 (not_1_out, Opcode[1]);
  not not_2 (not_2_out, Opcode[0]);
  not not_3 (not_3_out, Opcode[3]);
  Comparator #(.mode("unsigned"), .width(6)) comparator_3 (
    .a(6'b001000), .b(Opcode), .eq(comparator_3_eq));  // open: gt, lt
  Comparator #(.width(6)) comparator_4 (.a(funct), .b(6'b001000), .eq(comparator_4_eq));  // open: gt, lt
  and and_1 (and_1_out, not_2_out, Opcode[1], not_3_out);
  Comparator #(.mode("unsigned"), .width(6)) comparator_5 (.a(6'b000011), .b(Opcode), .eq(is_jal));  // open: gt, lt
  Control_Alu alu_controler (.Opcode(Opcode), .funct(funct), .aluop(aluop));
  and and_2 (bne, Opcode[0], not_1_out, Opcode[2]);
  or or_2 (jump, and_1_out, is_jal);
  not not_4 (not_4_out, funct[3]);
  Comparator #(.mode("unsigned"), .width(6)) comparator_6 (
    .a(Opcode), .b(6'b100011), .eq(comparator_6_eq));  // open: gt, lt
  Comparator #(.mode("unsigned"), .width(6)) comparator_7 (.a(Opcode), .b(6'b001010), .eq(slti));  // open: gt, lt
  Comparator #(.mode("unsigned"), .width(6)) comparator_8 (
    .a({6{1'b0}}), .b(funct), .eq(comparator_8_eq));  // open: gt, lt
  Comparator #(.mode("unsigned"), .width(6)) comparator_9 ();  // open: a, b, gt, eq, lt
  not not_5 (regdst, Rtype);
  and and_3 (mf, Rtype, not_4_out, funct[4]);
  Comparator #(.mode("unsigned"), .width(6)) comparator_10 (.a(6'b101011), .b(Opcode), .eq(mem_write));  // open: gt, lt
  or or_3 (or_3_out, comparator_3_eq, Rtype, comparator_6_eq, slti);
  Comparator #(.mode("unsigned"), .width(6)) comparator_11 (
    .a(funct), .b(6'b011010), .eq(comparator_11_eq));  // open: gt, lt
  Comparator #(.width(6)) comparator_12 (.a(Opcode), .b(6'b011100), .eq(comparator_12_eq));  // open: gt, lt
  Comparator #(.width(6)) comparator_13 (.a(funct), .b(6'b000010), .eq(comparator_13_eq));  // open: gt, lt
  Comparator #(.width(6)) comparator_14 (.a(Opcode), .b(6'b000100), .eq(beq));  // open: gt, lt
  Comparator #(.mode("unsigned"), .width(6)) comparator_15 (
    .a(6'b000101), .b(Opcode), .eq(comparator_15_eq));  // open: gt, lt
  Comparator #(.mode("unsigned"), .width(6)) comparator_16 (
    .a(6'b001000), .b(Opcode), .eq(comparator_16_eq));  // open: gt, lt
  not not_6 (not_6_out, is_div);
  and and_4 (sll_control, Rtype, comparator_8_eq);
  and and_5 (is_div, Rtype, comparator_11_eq);
  and and_6 (is_mul, comparator_12_eq, comparator_13_eq);
  not not_7 (not_7_out, comparator_12_eq);
  not not_8 (not_8_out, comparator_15_eq);
  not not_9 (not_9_out, comparator_16_eq);
  and and_7 (reg_write, or_3_out, not_6_out);
  and and_8 (is_jr, Rtype, comparator_4_eq);
  and and_9 (source_2, regdst, not_7_out, not_8_out);
  and and_10 (mem_to_reg, regdst, not_9_out);

  assign lo_or_hi = funct[1];
endmodule

module handle_inst_done (
  input  done,
  input  [3:0] aluop,
  input  is_div,
  input  is_mul,
  input  clk,
  input  rst,
  output inst_done
);

  wire and_1_out, comparator_1_eq, not_1_out, or_1_out;
  wire [3:0] register_1_q;

  Register #(.width(4)) register_1 (.D(aluop), .en(1'b1), .clk(clk), .Q(register_1_q), .clr(rst));
  Comparator #(.mode("unsigned"), .width(4)) comparator_1 (
    .a(register_1_q), .b(aluop), .eq(comparator_1_eq));  // open: gt, lt
  not not_1 (not_1_out, comparator_1_eq);
  or or_1 (or_1_out, is_mul, is_div);
  and and_1 (and_1_out, not_1_out, or_1_out);
  Multiplexer multiplexer_1 (.in0(done), .in1(1'b0), .out(inst_done), .sel(and_1_out));
endmodule

module Onehot (
  input  Instdone,
  input  rst,
  input  clk,
  output IFetch,
  output Exec,
  output Mem,
  output WB,
  output IDecode
);

  wire and_1_out, and_2_out, multiplexer_1_out, not_1_out;

  D_Flip_Flop d_ff_1 (.D(WB), .clk(clk), .Q(IFetch), .preset(rst));  // open: Qn, reset
  D_Flip_Flop d_ff_2 (.D(IFetch), .clk(clk), .Q(IDecode), .reset(rst));  // open: Qn, preset
  Multiplexer multiplexer_1 (.in0(IDecode), .in1(Exec), .out(multiplexer_1_out), .sel(and_1_out));
  not not_1 (not_1_out, Instdone);
  D_Flip_Flop d_ff_3 (.D(multiplexer_1_out), .clk(clk), .Q(Exec), .reset(rst));  // open: Qn, preset
  and and_1 (and_1_out, not_1_out, Exec);
  and and_2 (and_2_out, Instdone, Exec);
  D_Flip_Flop d_ff_4 (.D(and_2_out), .clk(clk), .Q(Mem), .reset(rst));  // open: Qn, preset
  D_Flip_Flop d_ff_5 (.D(Mem), .clk(clk), .Q(WB), .reset(rst));  // open: Qn, preset
endmodule
